// Logisim project BigASM (1) (3).circ as structural Verilog
module BOARD_BIG_ASM (
  output out_1
);

  wire button_1_out, CLK, CLR, d_ff_1_q, not_1_out, Write, Write_ASCII;
  wire [6:0] ASCII;
  wire [7:0] counter_1_q;
  wire [23:0] Dir_INPUT, Dir_MEMORY;
  wire [31:0] INPUT, MEMORY_IN, MEMORY_OUT;

  Button button_1 (.out(button_1_out));
  Clock clock_1 (.out(CLK));
  D_Flip_Flop d_ff_1 (.clk(CLK), .D(1'b1), .Q(d_ff_1_q), .reset(button_1_out));  // open: Qn, preset, en
  D_Flip_Flop d_ff_2 (.clk(CLK), .D(d_ff_1_q), .Qn(CLR), .reset(button_1_out));  // open: Q, preset, en
  BIG_ASM big_asm_1 (
    .DATA_INPUT(INPUT), .MEMORY_IN(MEMORY_OUT), .CLK(CLK), .CLR(CLR), .DIR_INPUT(Dir_INPUT),
    .MEMORY_OUT(MEMORY_IN), .DIR_MEMORY(Dir_MEMORY), .Write_OUTPUT(Write), .ASCII(ASCII),
    .Write_ASCII(Write_ASCII), .END(out_1));
  MEMORY memory_1 (.DIR(Dir_MEMORY), .DATA_IN(MEMORY_IN), .WRITE(Write), .CLK(CLK), .CLR(CLR), .DATA_OUT(MEMORY_OUT));
  INPUT input_1 (.DIR(Dir_INPUT), .CLK(CLK), .DATA_OUT(INPUT));
  Counter counter_1 (.load(1'b0), .count(not_1_out), .Q(counter_1_q), .clk(CLK), .clr(CLR));  // open: D, carry
  not not_1 (not_1_out, out_1);
  // Probe on counter_1_q
  TTY #(.rows(32), .cols(60)) tty_1 (.data(ASCII), .clk(CLK), .we(Write_ASCII), .clr(CLR));

  // Other names for the same wires on the sheet: END = out_1

  // Notes on the sheet:
  //   COUNTER
  //   BOARD
endmodule

module INPUT (
  input  [23:0] DIR,
  input  CLK,
  output [31:0] DATA_OUT
);

  RAM #(.addrWidth(24), .dataWidth(32)) ram_1 (.addr(DIR), .data(DATA_OUT), .clk(CLK), .ld(1'b1));  // open: sel, clr
endmodule

module MEMORY (
  input  [23:0] DIR,
  input  [31:0] DATA_IN,
  input  WRITE,
  input  CLK,
  input  CLR,
  output [31:0] DATA_OUT
);

  RAM #(.addrWidth(24), .dataWidth(32), .bus("separate")) ram_1 (
    .addr(DIR), .din(DATA_IN), .data(DATA_OUT), .str(WRITE), .clk(CLK), .clr(CLR));  // open: sel, ld
endmodule

module BIG_ASM (
  input  [31:0] DATA_INPUT,
  input  [31:0] MEMORY_IN,
  input  CLK,
  input  CLR,
  output [23:0] DIR_INPUT,
  output [31:0] MEMORY_OUT,
  output [23:0] DIR_MEMORY,
  output Write_OUTPUT,
  output [6:0] ASCII,
  output Write_ASCII,
  output END
);

  Counter #(.width(24), .max('hffffff)) counter_1 (.Q(DIR_INPUT), .clk(CLK), .clr(CLR));  // open: load, D, count, carry

  // Other names for the same wires on the sheet: Counter[23:0] = DIR_INPUT; IN[15:0] = DATA_INPUT[15:0]
endmodule

module PRINT_UDEC (
  input  [31:0] num,
  input  start,
  input  CLK,
  input  RST,
  output [6:0] ASCII,
  output Write_ASCII,
  output \end 
);

  wire _0_c, _0_n, demultiplexer_1_out0, demultiplexer_2_out0, demultiplexer_2_out1, demultiplexer_3_out0,
       demultiplexer_3_out1, IDLE_2_q, IDLE_3_q, IDLE_4_q, IDLE_q, Lc, Lc_0, Ln, Ln_0, or_1_out;
  wire [23:0] bit_extender_1_out;
  wire [31:0] c, c___1, c___1_t, divider_1_rem, memory_1_data_out, multiplexer_1_out, multiplexer_2_out,
       multiplexer_3_out, n, n___10, n___10___48;

  Multiplexer #(.width(32), .enable("false")) multiplexer_1 (
    .in0(num), .in1(n___10), .out(multiplexer_1_out), .sel(Lc_0));
  Divider #(.width(32)) divider_1 (.a(n), .b(32'ha), .out(n___10), .rem(divider_1_rem));  // open: upper
  Adder #(.width(32)) adder_1 (.a(divider_1_rem), .b(32'h30), .out(n___10___48));  // open: cin, cout
  or or_1 (or_1_out, demultiplexer_1_out0, \end );
  Register #(.width(32)) u_n (.D(multiplexer_1_out), .en(Ln), .Q(n), .clk(CLK), .clr(RST));
  D_Flip_Flop IDLE (.clk(CLK), .D(or_1_out), .Q(IDLE_q), .preset(RST));  // open: Qn, en, reset
  Demultiplexer #(.enable("false")) demultiplexer_1 (
    .out0(demultiplexer_1_out0), .out1(Ln_0), .in(IDLE_q), .sel(start));
  or or_2 (Write_ASCII, demultiplexer_3_out0, demultiplexer_2_out1);
  Multiplexer #(.width(32), .enable("false")) multiplexer_2 (
    .in0(c___1), .in1(c___1_t), .out(multiplexer_2_out), .sel(Write_ASCII));
  Adder #(.width(32)) adder_2 (.a(c), .b(32'h1), .out(c___1));  // open: cin, cout
  Subtractor #(.width(32)) subtractor_1 (.a(c), .b(32'h1), .out(c___1_t));  // open: bin, bout
  D_Flip_Flop IDLE_2 (.clk(CLK), .D(Ln_0), .Q(IDLE_2_q), .reset(RST));  // open: Qn, preset, en
  Register #(.width(32)) u_c (.D(multiplexer_2_out), .en(Lc), .Q(c), .clk(CLK), .clr(RST));
  or or_3 (Lc_0, IDLE_2_q, demultiplexer_3_out1);
  Multiplexer #(.width(32), .enable("false")) multiplexer_3 (
    .in0(c), .in1(c___1_t), .out(multiplexer_3_out), .sel(Write_ASCII));
  Comparator #(.width(32), .mode("unsigned")) comparator_1 (.a({32{1'b0}}), .b(n), .lt(_0_n));  // open: gt, eq
  Comparator #(.width(32), .mode("unsigned")) comparator_2 (.a({32{1'b0}}), .b(c), .lt(_0_c));  // open: gt, eq
  D_Flip_Flop IDLE_3 (.clk(CLK), .D(Write_ASCII), .Q(IDLE_3_q), .reset(RST));  // open: Qn, preset, en
  Demultiplexer #(.enable("false")) demultiplexer_2 (
    .out0(demultiplexer_2_out0), .out1(demultiplexer_2_out1), .in(IDLE_3_q), .sel(_0_c));
  Bit_Extender #(.in_width(32), .out_width(24)) bit_extender_1 (.in(multiplexer_3_out), .out(bit_extender_1_out));
  D_Flip_Flop IDLE_4 (.clk(CLK), .D(Lc_0), .Q(IDLE_4_q), .reset(RST));  // open: Qn, preset, en
  or or_4 (Lc, Lc_0, Write_ASCII);
  or or_5 (Ln, Ln_0, Lc_0);
  Demultiplexer #(.enable("false")) demultiplexer_3 (
    .out0(demultiplexer_3_out0), .out1(demultiplexer_3_out1), .in(IDLE_4_q), .sel(_0_n));
  D_Flip_Flop IDLE_5 (.clk(CLK), .D(demultiplexer_2_out0), .Q(\end ), .reset(RST));  // open: Qn, preset, en
  MEMORY memory_1 (
    .DIR(bit_extender_1_out), .DATA_IN(n___10___48), .WRITE(Lc_0), .CLK(CLK), .CLR(RST),
    .DATA_OUT(memory_1_data_out));
  Bit_Extender #(.in_width(32), .out_width(7)) bit_extender_2 (.in(memory_1_data_out), .out(ASCII));

  // Other names for the same wires on the sheet: Lc_1 = Write_ASCII; Sc = Write_ASCII; Ln_1 = Lc_0; Sn = Lc_0;
  //   Write = Lc_0
endmodule

module PRINT_DEC (
  input  [31:0] num,
  input  start,
  input  CLK,
  input  RST,
  output [6:0] ASCII,
  output Write_ASCII,
  output END
);

  wire demultiplexer_1_out0, demultiplexer_1_out1, demultiplexer_2_out0, demultiplexer_3_out0, end_t,
       IDLE_3_q, IDLE_q, or_1_out, or_2_out, or_3_out, S_ASCII, startUDEC, Write_ASCII_1;
  wire [6:0] ASCII_t;
  wire [31:0] multiplexer_1_out, negator_1_out;

  or or_1 (or_1_out, demultiplexer_1_out0, END);
  Negator #(.width(32)) negator_1 (.in(num), .out(negator_1_out));
  D_Flip_Flop IDLE (.clk(CLK), .D(or_1_out), .Q(IDLE_q), .preset(RST));  // open: Qn, en, reset
  Demultiplexer #(.enable("false")) demultiplexer_1 (
    .out0(demultiplexer_1_out0), .out1(demultiplexer_1_out1), .in(IDLE_q), .sel(start));
  Multiplexer #(.width(32), .enable("false")) multiplexer_1 (
    .in0(num), .in1(negator_1_out), .out(multiplexer_1_out), .sel(num[31]));
  Demultiplexer #(.enable("false")) demultiplexer_2 (
    .out0(demultiplexer_2_out0), .out1(S_ASCII), .in(demultiplexer_1_out1), .sel(num[31]));
  or or_2 (or_2_out, demultiplexer_2_out0, S_ASCII);
  D_Flip_Flop IDLE_2 (.clk(CLK), .D(or_2_out), .Q(startUDEC), .reset(RST));  // open: Qn, preset, en
  PRINT_UDEC print_udec_1 (
    .num(multiplexer_1_out), .start(startUDEC), .CLK(CLK), .RST(RST), .ASCII(ASCII_t),
    .Write_ASCII(Write_ASCII_1), .\end (end_t));
  D_Flip_Flop IDLE_3 (.clk(CLK), .D(or_3_out), .Q(IDLE_3_q), .reset(RST));  // open: Qn, preset, en
  or or_3 (or_3_out, startUDEC, demultiplexer_3_out0);
  Demultiplexer #(.enable("false")) demultiplexer_3 (
    .out0(demultiplexer_3_out0), .out1(END), .in(IDLE_3_q), .sel(end_t));
  Multiplexer #(.width(7), .enable("false")) multiplexer_2 (
    .in0(ASCII_t), .in1(7'b0101101), .out(ASCII), .sel(S_ASCII));
  or or_4 (Write_ASCII, S_ASCII, Write_ASCII_1);

  // Other names for the same wires on the sheet: sign = num[31]; Write_ASCII_0 = S_ASCII
endmodule

module TEST_PRINT (
  input  [31:0] in_1,
  output out_2
);

  wire button_1_out, button_2_out, CLK, CLR, d_ff_1_q, Write_ASCII;
  wire [6:0] ASCII;

  Button button_1 (.out(button_1_out));
  Clock clock_1 (.out(CLK));
  D_Flip_Flop d_ff_1 (.clk(CLK), .D(1'b1), .Q(d_ff_1_q), .reset(button_1_out));  // open: Qn, preset, en
  D_Flip_Flop d_ff_2 (.clk(CLK), .D(d_ff_1_q), .Qn(CLR), .reset(button_1_out));  // open: Q, preset, en
  Button button_2 (.out(button_2_out));
  PRINT_UDEC print_udec_1 ();  // open: num, start, CLK, RST, ASCII, Write_ASCII, end
  PRINT_DEC print_dec_1 (
    .num(in_1), .start(button_2_out), .CLK(CLK), .RST(CLR), .ASCII(ASCII), .Write_ASCII(Write_ASCII),
    .END(out_2));
  TTY #(.rows(32), .cols(60)) tty_1 (.data(ASCII), .clk(CLK), .we(Write_ASCII), .clr(CLR));
endmodule

module IsPrime_Control_Unit (
  input  in_1,
  input  in_2,
  input  Clock,
  output out_4
);

  wire d_ff_1_q, d_ff_3_q, demultiplexer_1_out0, demultiplexer_2_out0, demultiplexer_2_out1,
       demultiplexer_3_out1, LC0, LC1, or_1_out, or_2_out, RESET, START;

  Demultiplexer #(.enable("false")) demultiplexer_1 (
    .out0(demultiplexer_1_out0), .out1(LC0), .in(d_ff_1_q), .sel(START));
  D_Flip_Flop d_ff_1 (.clk(Clock), .D(demultiplexer_1_out0), .Q(d_ff_1_q), .preset(RESET));  // open: Qn, en, reset
  D_Flip_Flop d_ff_2 (.Q(START), .Qn(RESET), .preset(Clock));  // open: clk, D, en, reset
  or or_1 (or_1_out, LC0, LC1);
  D_Flip_Flop d_ff_3 (.clk(Clock), .D(or_1_out), .Q(d_ff_3_q), .reset(RESET));  // open: Qn, preset, en
  Demultiplexer #(.enable("false")) demultiplexer_2 (
    .out0(demultiplexer_2_out0), .out1(demultiplexer_2_out1), .in(d_ff_3_q), .sel(in_1));
  Demultiplexer #(.enable("false")) demultiplexer_3 (
    .out0(LC1), .out1(demultiplexer_3_out1), .in(demultiplexer_2_out1), .sel(in_2));
  or or_2 (or_2_out, demultiplexer_2_out0, demultiplexer_3_out1);
  D_Flip_Flop d_ff_4 (.clk(Clock), .D(or_2_out), .Q(out_4), .reset(RESET));  // open: Qn, preset, en

  // Other names for the same wires on the sheet: C___N = in_1; CLK = Clock; N___C____0 = in_2; SC = LC1
endmodule

module IsPrime_DataPath (
  input  [31:0] INPUT,
  input  CLK,
  input  Selector_Ctor,
  input  L_Ctor,
  input  L_Registro,
  output Resultado,
  output Ctor_Input,
  output Input_Ctor__0
);

  wire [31:0] Ctor, Ctor__1, Input_Ctor, multiplexer_1_out;

  Multiplexer #(.width(32)) multiplexer_1 (
    .in0(32'h2), .in1(Ctor__1), .out(multiplexer_1_out), .en(Selector_Ctor));  // open: sel
  Adder #(.width(32)) adder_1 (.a(Ctor), .b(32'h1), .out(Ctor__1));  // open: cin, cout
  Divider #(.width(32)) divider_1 (.a(INPUT), .b(Ctor), .rem(Input_Ctor));  // open: out, upper
  Register #(.width(32)) Contador (.D(multiplexer_1_out), .en(L_Ctor), .Q(Ctor), .clk(CLK));  // open: clr
  Register #(.width(1)) u_Resultado (.D(Input_Ctor__0), .en(L_Registro), .Q(Resultado), .clk(CLK));  // open: clr
  Comparator #(.width(32)) comparator_1 (.a(Ctor), .b(INPUT), .lt(Ctor_Input));  // open: gt, eq
  Comparator #(.width(32)) comparator_2 (.a(Input_Ctor), .b({32{1'b0}}), .eq(Input_Ctor__0));  // open: gt, lt

  // Other names for the same wires on the sheet: Input_Ctor____0 = Input_Ctor__0; L_C = L_Ctor
endmodule

module PerfectNumber_DataPath (
  input  [31:0] \input ,
  input  [31:0] Numero_Perfecto,
  input  Load_numerp_Perfecto,
  input  Load_Contador,
  input  CLK,
  input  [1:0] Selector,
  output Ctor__Input
);

  wire [31:0] _2___m_1, Contador, Contador___1, Mersenne, mersenne_asm_1_nummersenne, multiplexer_1_out,
       numero_perfecto_t;

  Mersenne_ASM mersenne_asm_1 (.\input (\input ), .in_2(CLK), .NumMersenne(mersenne_asm_1_nummersenne));
  Multiplier #(.width(32)) multiplier_1 (.a(Numero_Perfecto), .b(32'h2), .out(_2___m_1));  // open: cin, cout
  Register #(.width(32)) register_1 (.D(Contador___1), .en(Load_Contador), .Q(Contador), .clk(CLK));  // open: clr
  Multiplier #(.width(32)) multiplier_2 (
    .a(Numero_Perfecto), .b(Mersenne), .out(numero_perfecto_t));  // open: cin, cout
  Register #(.width(32)) numero_Mersenne (.D(mersenne_asm_1_nummersenne), .Q(Mersenne), .clk(CLK));  // open: en, clr
  Multiplexer #(.select(2), .width(32), .enable("false")) multiplexer_1 (
    .in0(32'h1), .in1(_2___m_1), .in2(numero_perfecto_t), .out(multiplexer_1_out), .sel(Selector));  // open: in3
  Comparator #(.width(32)) comparator_1 (.a(Contador), .b(\input ), .eq(Ctor__Input));  // open: gt, lt
  Register #(.width(32)) u_Numero_Perfecto (
    .D(multiplexer_1_out), .en(Load_numerp_Perfecto), .Q(Numero_Perfecto), .clk(CLK));  // open: clr

  // Other names for the same wires on the sheet: L_contador = Load_Contador; L_numPerf = Load_numerp_Perfecto;
  //   num_Perf[31:0] = Numero_Perfecto; Selector_de_2__m_1[1:0] = Selector

  // Notes on the sheet:
  //   2**(m-1) * 2**m -1
endmodule

module Mersenne_DataPath (
  input  [31:0] \input ,
  input  L_Ctor,
  input  [1:0] Selector_2__t,
  input  L_2__t,
  input  CLK,
  output [31:0] num_mersenne,
  output Cond_Ctor__Input
);

  wire [31:0] _2x2___t_1, Ctor, Ctor__1, Mersenne, multiplexer_1_out;

  // Probe on 32'h2
  Multiplexer #(.select(2), .width(32), .enable("false")) multiplexer_1 (
    .in0(32'h2), .in1(_2x2___t_1), .in2(Mersenne), .out(multiplexer_1_out), .sel(Selector_2__t));  // open: in3
  Register #(.width(32)) _2__ctor (.D(multiplexer_1_out), .en(L_2__t), .Q(num_mersenne), .clk(CLK));  // open: clr
  Multiplier #(.width(32)) multiplier_1 (.a(num_mersenne), .b(32'h2), .out(_2x2___t_1));  // open: cin, cout
  Subtractor #(.width(32)) subtractor_1 (.a(num_mersenne), .b(32'h1), .out(Mersenne));  // open: bin, bout
  Adder #(.width(32)) adder_1 (.a(Ctor), .b(32'h1), .out(Ctor__1));  // open: cin, cout
  Register #(.width(32)) u_ctor (.D(Ctor__1), .en(L_Ctor), .Q(Ctor), .clk(CLK));  // open: clr
  Comparator #(.width(32)) comparator_1 (.a(Ctor), .b(\input ), .eq(Cond_Ctor__Input));  // open: gt, lt

  // Other names for the same wires on the sheet: _2__ctor[31:0] = num_mersenne; Ctor____input = Cond_Ctor__Input;
  //   L_2__ctor = L_2__t

  // Notes on the sheet:
  //   (2**m)
  //   -1
endmodule

module Mersenne_Control_Unit (
  input  C____N,
  input  Clock,
  output END,
  output LC,
  output L2_t,
  output [1:0] S2_t
);

  wire d_ff_1_q, d_ff_4_q, d_ff_6_q, demultiplexer_1_out0, L02_t, LC0, LC1, or_1_out, RESET, START;

  D_Flip_Flop d_ff_1 (.clk(Clock), .D(demultiplexer_1_out0), .Q(d_ff_1_q), .preset(RESET));  // open: Qn, en, reset
  Demultiplexer #(.enable("false")) demultiplexer_1 (
    .out0(demultiplexer_1_out0), .out1(LC0), .in(d_ff_1_q), .sel(START));
  D_Flip_Flop d_ff_2 (.Q(START), .Qn(RESET), .preset(Clock));  // open: clk, D, en, reset
  D_Flip_Flop d_ff_3 (.clk(Clock), .D(LC0), .Q(L02_t), .reset(RESET));  // open: Qn, preset, en
  or or_1 (or_1_out, L02_t, d_ff_6_q);
  D_Flip_Flop d_ff_4 (.clk(Clock), .D(or_1_out), .Q(d_ff_4_q), .reset(RESET));  // open: Qn, preset, en
  Demultiplexer #(.enable("false")) demultiplexer_2 (.out0(S2_t[0]), .out1(S2_t[1]), .in(d_ff_4_q), .sel(C____N));
  or or_2 (LC, LC0, LC1);
  or or_3 (L2_t, L02_t, S2_t[0], S2_t[1]);
  D_Flip_Flop d_ff_5 (.clk(Clock), .D(S2_t[0]), .Q(LC1), .reset(RESET));  // open: Qn, preset, en
  D_Flip_Flop d_ff_6 (.clk(Clock), .D(LC1), .Q(d_ff_6_q), .reset(RESET));  // open: Qn, preset, en
  D_Flip_Flop d_ff_7 (.clk(Clock), .D(S2_t[1]), .Q(END), .reset(RESET));  // open: Qn, preset, en

  // Other names for the same wires on the sheet: CLK = Clock; L12_t = S2_t[0]; S01_2_t = S2_t[0]; L22_t = S2_t[1];
  //   S10_2_t = S2_t[1]

  // Notes on the sheet:
  //   IDLE
  //   WHILE
endmodule

module PerfectNumber_Control_Unit (
  input  IsPrime_m____IsPrime_Mersenne,
  input  C___N,
  input  Clock,
  output END,
  output LM,
  output LC,
  output LPN
);

  wire d_ff_1_q, d_ff_4_q, d_ff_7_q, demultiplexer_1_out0, demultiplexer_2_out0, demultiplexer_2_out1,
       demultiplexer_3_out0, LC0, LC1, LM0, LM1, or_1_out, RESET, START;

  D_Flip_Flop d_ff_1 (.clk(Clock), .D(demultiplexer_1_out0), .Q(d_ff_1_q), .preset(RESET));  // open: Qn, en, reset
  Demultiplexer demultiplexer_1 (.out0(demultiplexer_1_out0), .out1(LM0), .in(d_ff_1_q), .sel(START));  // open: en
  D_Flip_Flop d_ff_2 (.Q(START), .Qn(RESET), .preset(Clock));  // open: clk, D, en, reset
  D_Flip_Flop d_ff_3 (.clk(Clock), .D(LM0), .Q(LC0), .reset(RESET));  // open: Qn, preset, en
  or or_1 (or_1_out, LC0, LM1);
  D_Flip_Flop d_ff_4 (.clk(Clock), .D(or_1_out), .Q(d_ff_4_q), .reset(RESET));  // open: Qn, preset, en
  Demultiplexer demultiplexer_2 (
    .out0(demultiplexer_2_out0), .out1(demultiplexer_2_out1), .in(d_ff_4_q), .sel(C___N));  // open: en
  Demultiplexer demultiplexer_3 (
    .out0(demultiplexer_3_out0), .out1(LPN), .in(demultiplexer_2_out1), .sel(IsPrime_m____IsPrime_Mersenne));  // open: en
  or or_2 (LM, LM0, LM1);
  or or_3 (LC, LC0, LC1);
  D_Flip_Flop d_ff_5 (.clk(Clock), .D(demultiplexer_2_out0), .Q(END), .reset(RESET));  // open: Qn, preset, en
  D_Flip_Flop d_ff_6 (.clk(Clock), .D(LPN), .Q(LC1), .reset(RESET));  // open: Qn, preset, en
  D_Flip_Flop d_ff_7 (.clk(Clock), .D(LC1), .Q(d_ff_7_q), .reset(RESET));  // open: Qn, preset, en
  or or_4 (LM1, demultiplexer_3_out0, d_ff_7_q);

  // Other names for the same wires on the sheet: CLK = Clock; SM = LM1
endmodule

module N_esimo_Numero_Perfecto_Datapath (
);

  wire CLK, L_Ctor, L_M, L_Mersenne, L_NumPerf;
  wire [31:0] Ctor, Ctor_1, \input , M, M_1, Mersenne, mersenne_asm_1_nummersenne, multiplexer_1_out,
       Numero_Perfecto, numero_perfecto_ARREGLAR;

  Multiplexer #(.width(32), .enable("false")) multiplexer_1 (
    .in0(32'h2), .in1(M_1), .out(multiplexer_1_out));  // open: sel
  Register #(.width(32)) u_M (.D(multiplexer_1_out), .en(L_M), .Q(M), .clk(CLK));  // open: clr
  Register #(.width(32)) Contador (.D(Ctor_1), .en(L_Ctor), .Q(Ctor), .clk(CLK));  // open: clr
  Mersenne_ASM mersenne_asm_1 (.\input (\input ), .in_2(CLK), .NumMersenne(mersenne_asm_1_nummersenne));
  Register #(.width(32)) u_Mersenne (
    .D(mersenne_asm_1_nummersenne), .en(L_Mersenne), .Q(Mersenne), .clk(CLK));  // open: clr
  Register #(.width(32)) u_Numero_Perfecto (
    .D(numero_perfecto_ARREGLAR), .en(L_NumPerf), .Q(Numero_Perfecto), .clk(CLK));  // open: clr
endmodule

module Mersenne_ASM (
  input  [31:0] \input ,
  input  in_2,
  output [31:0] NumMersenne
);

  wire END, mersenne_control_unit_1_l2_t, mersenne_control_unit_1_lc, mersenne_datapath_1_cond_ctor__input;
  wire [1:0] mersenne_control_unit_1_s2_t;

  Mersenne_Control_Unit mersenne_control_unit_1 (
    .C____N(mersenne_datapath_1_cond_ctor__input), .Clock(in_2), .END(END), .LC(mersenne_control_unit_1_lc),
    .L2_t(mersenne_control_unit_1_l2_t), .S2_t(mersenne_control_unit_1_s2_t));
  Mersenne_DataPath mersenne_datapath_1 (
    .\input (\input ), .CLK(in_2), .L_2__t(mersenne_control_unit_1_l2_t),
    .L_Ctor(mersenne_control_unit_1_lc), .num_mersenne(NumMersenne),
    .Cond_Ctor__Input(mersenne_datapath_1_cond_ctor__input), .Selector_2__t(mersenne_control_unit_1_s2_t));

  // Other names for the same wires on the sheet: CLK = in_2; Num_Mersene[31:0] = NumMersenne
endmodule
