// Logisim project BigASM.circ as structural Verilog
module BOARD_BIG_ASM (
  output out_1
);

  wire button_1_out, CLK, CLR, d_ff_1_q, not_1_out, Write, Write_ASCII;
  wire [6:0] ASCII;
  wire [7:0] counter_1_q;
  wire [23:0] Dir_INPUT, Dir_MEMORY;
  wire [31:0] INPUT, MEMORY_IN, MEMORY_OUT;

  Button button_1 (.out(button_1_out));
  Clock clock_1 (.out(CLK));
  D_Flip_Flop d_ff_1 (.clk(CLK), .D(1'b1), .Q(d_ff_1_q), .reset(button_1_out));  // open: Qn, preset, en
  D_Flip_Flop d_ff_2 (.clk(CLK), .D(d_ff_1_q), .Qn(CLR), .reset(button_1_out));  // open: Q, preset, en
  BIG_ASM big_asm_1 (
    .DATA_INPUT(INPUT), .MEMORY_IN(MEMORY_OUT), .CLR(CLR), .DIR_INPUT(Dir_INPUT), .MEMORY_OUT(MEMORY_IN),
    .DIR_MEMORY(Dir_MEMORY), .Write_OUTPUT(Write), .ASCII(ASCII), .Write_ASCII(Write_ASCII), .END(out_1),
    .CLK(CLK));
  MEMORY memory_1 (.DIR(Dir_MEMORY), .DATA_IN(MEMORY_IN), .WRITE(Write), .CLK(CLK), .CLR(CLR), .DATA_OUT(MEMORY_OUT));
  INPUT input_1 (.DIR(Dir_INPUT), .CLK(CLK), .DATA_OUT(INPUT));
  Counter counter_1 (.load(1'b0), .count(not_1_out), .Q(counter_1_q), .clk(CLK), .clr(CLR));  // open: D, carry
  not not_1 (not_1_out, out_1);
  // Probe on counter_1_q
  TTY #(.rows(32), .cols(60)) tty_1 (.data(ASCII), .clk(CLK), .we(Write_ASCII), .clr(CLR));

  // Other names for the same wires on the sheet: END = out_1

  // Notes on the sheet:
  //   COUNTER
  //   BOARD
endmodule

module INPUT (
  input  [23:0] DIR,
  input  CLK,
  output [31:0] DATA_OUT
);

  RAM #(.addrWidth(24), .dataWidth(32)) ram_1 (.addr(DIR), .data(DATA_OUT), .clk(CLK), .ld(1'b1));  // open: sel, clr
endmodule

module MEMORY (
  input  [23:0] DIR,
  input  [31:0] DATA_IN,
  input  WRITE,
  input  CLK,
  input  CLR,
  output [31:0] DATA_OUT
);

  RAM #(.addrWidth(24), .dataWidth(32), .bus("separate")) ram_1 (
    .addr(DIR), .din(DATA_IN), .data(DATA_OUT), .str(WRITE), .clk(CLK), .clr(CLR));  // open: sel, ld
endmodule

module BIG_ASM (
  input  [31:0] DATA_INPUT,
  input  [31:0] MEMORY_IN,
  input  CLK,
  input  CLR,
  output [23:0] DIR_INPUT,
  output [31:0] MEMORY_OUT,
  output [23:0] DIR_MEMORY,
  output Write_OUTPUT,
  output [6:0] ASCII,
  output Write_ASCII,
  output END
);

  wire d_ff_1_q, END_t, nth_perfect_number_datapath_1_contador__input, nth_perfectnumber_control_unit_1_clr,
       nth_perfectnumber_control_unit_1_lc, nth_perfectnumber_control_unit_1_lin,
       nth_perfectnumber_control_unit_1_lm, nth_perfectnumber_control_unit_1_sm;
  wire [31:0] nth_perfect_number_datapath_1_m, nth_perfectnumber_control_unit_1_perfect_number, Result;

  Counter #(.width(24), .max('hffffff)) counter_1 (.Q(DIR_INPUT), .clk(CLK), .clr(CLR));  // open: load, D, count, carry
  Nth_Perfect_Number_DataPath nth_perfect_number_datapath_1 (
    .Selector_M(nth_perfectnumber_control_unit_1_sm), .L_M(nth_perfectnumber_control_unit_1_lm),
    .L_Contador(nth_perfectnumber_control_unit_1_lc), .END(END_t), .CLK(CLK),
    .Contador__Input(nth_perfect_number_datapath_1_contador__input), .M(nth_perfect_number_datapath_1_m),
    .Result(Result), .Perfect_Number(nth_perfectnumber_control_unit_1_perfect_number),
    .CLR(nth_perfectnumber_control_unit_1_clr), .INPUT(DATA_INPUT), .LIN(nth_perfectnumber_control_unit_1_lin));
  Nth_PerfectNumber_Control_Unit nth_perfectnumber_control_unit_1 (
    .Contador___Input(nth_perfect_number_datapath_1_contador__input), .END(END_t),
    .LM(nth_perfectnumber_control_unit_1_lm), .LC(nth_perfectnumber_control_unit_1_lc), .Clock(CLK),
    .M(nth_perfect_number_datapath_1_m), .Perfect_Number(nth_perfectnumber_control_unit_1_perfect_number),
    .SM(nth_perfectnumber_control_unit_1_sm), .CLR(nth_perfectnumber_control_unit_1_clr),
    .LIN(nth_perfectnumber_control_unit_1_lin));
  // Probe on Result
  // Probe on Result
  D_Flip_Flop d_ff_1 (.clk(CLK), .D(END_t), .Q(d_ff_1_q));  // open: Qn, preset, en, reset
  PRINT_DEC print_dec_1 (
    .num(Result), .start(d_ff_1_q), .CLK(CLK), .RST(CLR), .ASCII(ASCII), .Write_ASCII(Write_ASCII), .END(END));

  // Other names for the same wires on the sheet: Counter[23:0] = DIR_INPUT; IN[31:0] = DATA_INPUT

  // Notes on the sheet:
  //   ARREGLAR RELOJ
endmodule

module PRINT_UDEC (
  input  [31:0] num,
  input  start,
  input  CLK,
  input  RST,
  output [6:0] ASCII,
  output Write_ASCII,
  output \end 
);

  wire _0_c, _0_n, demultiplexer_1_out0, demultiplexer_2_out0, demultiplexer_2_out1, demultiplexer_3_out0,
       demultiplexer_3_out1, IDLE_2_q, IDLE_3_q, IDLE_4_q, IDLE_q, Lc, Lc_0, Ln, Ln_0, or_1_out;
  wire [23:0] bit_extender_1_out;
  wire [31:0] c, c___1, c___1_t, divider_1_rem, memory_1_data_out, multiplexer_1_out, multiplexer_2_out,
       multiplexer_3_out, n, n___10, n___10___48;

  Multiplexer #(.width(32), .enable("false")) multiplexer_1 (
    .in0(num), .in1(n___10), .out(multiplexer_1_out), .sel(Lc_0));
  Divider #(.width(32)) divider_1 (.a(n), .b(32'ha), .out(n___10), .rem(divider_1_rem));  // open: upper
  Adder #(.width(32)) adder_1 (.a(divider_1_rem), .b(32'h30), .out(n___10___48));  // open: cin, cout
  or or_1 (or_1_out, demultiplexer_1_out0, \end );
  Register #(.width(32)) u_n (.D(multiplexer_1_out), .en(Ln), .Q(n), .clk(CLK), .clr(RST));
  D_Flip_Flop IDLE (.clk(CLK), .D(or_1_out), .Q(IDLE_q), .preset(RST));  // open: Qn, en, reset
  Demultiplexer #(.enable("false")) demultiplexer_1 (
    .out0(demultiplexer_1_out0), .out1(Ln_0), .in(IDLE_q), .sel(start));
  or or_2 (Write_ASCII, demultiplexer_3_out0, demultiplexer_2_out1);
  Multiplexer #(.width(32), .enable("false")) multiplexer_2 (
    .in0(c___1), .in1(c___1_t), .out(multiplexer_2_out), .sel(Write_ASCII));
  Adder #(.width(32)) adder_2 (.a(c), .b(32'h1), .out(c___1));  // open: cin, cout
  Subtractor #(.width(32)) subtractor_1 (.a(c), .b(32'h1), .out(c___1_t));  // open: bin, bout
  D_Flip_Flop IDLE_2 (.clk(CLK), .D(Ln_0), .Q(IDLE_2_q), .reset(RST));  // open: Qn, preset, en
  Register #(.width(32)) u_c (.D(multiplexer_2_out), .en(Lc), .Q(c), .clk(CLK), .clr(RST));
  or or_3 (Lc_0, IDLE_2_q, demultiplexer_3_out1);
  Multiplexer #(.width(32), .enable("false")) multiplexer_3 (
    .in0(c), .in1(c___1_t), .out(multiplexer_3_out), .sel(Write_ASCII));
  Comparator #(.width(32), .mode("unsigned")) comparator_1 (.a({32{1'b0}}), .b(n), .lt(_0_n));  // open: gt, eq
  Comparator #(.width(32), .mode("unsigned")) comparator_2 (.a({32{1'b0}}), .b(c), .lt(_0_c));  // open: gt, eq
  D_Flip_Flop IDLE_3 (.clk(CLK), .D(Write_ASCII), .Q(IDLE_3_q), .reset(RST));  // open: Qn, preset, en
  Demultiplexer #(.enable("false")) demultiplexer_2 (
    .out0(demultiplexer_2_out0), .out1(demultiplexer_2_out1), .in(IDLE_3_q), .sel(_0_c));
  Bit_Extender #(.in_width(32), .out_width(24)) bit_extender_1 (.in(multiplexer_3_out), .out(bit_extender_1_out));
  D_Flip_Flop IDLE_4 (.clk(CLK), .D(Lc_0), .Q(IDLE_4_q), .reset(RST));  // open: Qn, preset, en
  or or_4 (Lc, Lc_0, Write_ASCII);
  or or_5 (Ln, Ln_0, Lc_0);
  Demultiplexer #(.enable("false")) demultiplexer_3 (
    .out0(demultiplexer_3_out0), .out1(demultiplexer_3_out1), .in(IDLE_4_q), .sel(_0_n));
  D_Flip_Flop IDLE_5 (.clk(CLK), .D(demultiplexer_2_out0), .Q(\end ), .reset(RST));  // open: Qn, preset, en
  MEMORY memory_1 (
    .DIR(bit_extender_1_out), .DATA_IN(n___10___48), .WRITE(Lc_0), .CLK(CLK), .CLR(RST),
    .DATA_OUT(memory_1_data_out));
  Bit_Extender #(.in_width(32), .out_width(7)) bit_extender_2 (.in(memory_1_data_out), .out(ASCII));

  // Other names for the same wires on the sheet: Lc_1 = Write_ASCII; Sc = Write_ASCII; Ln_1 = Lc_0; Sn = Lc_0;
  //   Write = Lc_0
endmodule

module PRINT_DEC (
  input  [31:0] num,
  input  start,
  input  CLK,
  input  RST,
  output [6:0] ASCII,
  output Write_ASCII,
  output END
);

  wire demultiplexer_1_out0, demultiplexer_1_out1, demultiplexer_2_out0, demultiplexer_3_out0, end_t,
       IDLE_3_q, IDLE_q, or_1_out, or_2_out, or_3_out, S_ASCII, startUDEC, Write_ASCII_1;
  wire [6:0] ASCII_t;
  wire [31:0] multiplexer_1_out, negator_1_out;

  or or_1 (or_1_out, demultiplexer_1_out0, END);
  Negator #(.width(32)) negator_1 (.in(num), .out(negator_1_out));
  D_Flip_Flop IDLE (.clk(CLK), .D(or_1_out), .Q(IDLE_q), .preset(RST));  // open: Qn, en, reset
  Demultiplexer #(.enable("false")) demultiplexer_1 (
    .out0(demultiplexer_1_out0), .out1(demultiplexer_1_out1), .in(IDLE_q), .sel(start));
  Multiplexer #(.width(32), .enable("false")) multiplexer_1 (
    .in0(num), .in1(negator_1_out), .out(multiplexer_1_out), .sel(num[31]));
  Demultiplexer #(.enable("false")) demultiplexer_2 (
    .out0(demultiplexer_2_out0), .out1(S_ASCII), .in(demultiplexer_1_out1), .sel(num[31]));
  or or_2 (or_2_out, demultiplexer_2_out0, S_ASCII);
  D_Flip_Flop IDLE_2 (.clk(CLK), .D(or_2_out), .Q(startUDEC), .reset(RST));  // open: Qn, preset, en
  PRINT_UDEC print_udec_1 (
    .num(multiplexer_1_out), .start(startUDEC), .CLK(CLK), .RST(RST), .ASCII(ASCII_t),
    .Write_ASCII(Write_ASCII_1), .\end (end_t));
  D_Flip_Flop IDLE_3 (.clk(CLK), .D(or_3_out), .Q(IDLE_3_q), .reset(RST));  // open: Qn, preset, en
  or or_3 (or_3_out, startUDEC, demultiplexer_3_out0);
  Demultiplexer #(.enable("false")) demultiplexer_3 (
    .out0(demultiplexer_3_out0), .out1(END), .in(IDLE_3_q), .sel(end_t));
  Multiplexer #(.width(7), .enable("false")) multiplexer_2 (
    .in0(ASCII_t), .in1(7'b0101101), .out(ASCII), .sel(S_ASCII));
  or or_4 (Write_ASCII, S_ASCII, Write_ASCII_1);

  // Other names for the same wires on the sheet: sign = num[31]; Write_ASCII_0 = S_ASCII
endmodule

module TEST_PRINT (
  input  [31:0] in_1,
  output out_2
);

  wire button_1_out, button_2_out, CLK, CLR, d_ff_1_q, Write_ASCII;
  wire [6:0] ASCII;

  Button button_1 (.out(button_1_out));
  Clock clock_1 (.out(CLK));
  D_Flip_Flop d_ff_1 (.clk(CLK), .D(1'b1), .Q(d_ff_1_q), .reset(button_1_out));  // open: Qn, preset, en
  D_Flip_Flop d_ff_2 (.clk(CLK), .D(d_ff_1_q), .Qn(CLR), .reset(button_1_out));  // open: Q, preset, en
  Button button_2 (.out(button_2_out));
  PRINT_UDEC print_udec_1 ();  // open: num, start, CLK, RST, ASCII, Write_ASCII, end
  PRINT_DEC print_dec_1 (
    .num(in_1), .start(button_2_out), .CLK(CLK), .RST(CLR), .ASCII(ASCII), .Write_ASCII(Write_ASCII),
    .END(out_2));
  TTY #(.rows(32), .cols(60)) tty_1 (.data(ASCII), .clk(CLK), .we(Write_ASCII), .clr(CLR));
endmodule

module Mersenne_DataPath (
  input  [31:0] \input ,
  input  L_Ctor,
  input  [1:0] Selector_2__t,
  input  L_2__t,
  input  CLK,
  input  End,
  input  CLR,
  output [31:0] num_mersenne,
  output Cond_Ctor__Input
);

  wire [31:0] _2__ctor, _2x2___t_1, Ctor, Ctor__1, Mersenne, multiplexer_1_out;

  // Probe on 32'h2
  Multiplexer #(.select(2), .width(32), .enable("false")) multiplexer_1 (
    .in0(32'h2), .in1(_2x2___t_1), .in2(Mersenne), .out(multiplexer_1_out), .sel(Selector_2__t));  // open: in3
  Register #(.width(32)) u__2__ctor (.D(multiplexer_1_out), .en(L_2__t), .Q(_2__ctor), .clk(CLK), .clr(CLR));
  Multiplier #(.width(32)) multiplier_1 (.a(_2__ctor), .b(32'h2), .out(_2x2___t_1));  // open: cin, cout
  Subtractor #(.width(32)) subtractor_1 (.a(_2__ctor), .b(32'h1), .out(Mersenne));  // open: bin, bout
  Adder #(.width(32)) adder_1 (.a(Ctor), .b(32'h1), .out(Ctor__1));  // open: cin, cout
  Register #(.width(32)) u_ctor (.D(Ctor__1), .en(L_Ctor), .Q(Ctor), .clk(CLK), .clr(CLR));
  Register #(.width(32)) register_1 (.D(_2__ctor), .en(End), .Q(num_mersenne), .clk(CLK));  // open: clr
  Comparator #(.width(32)) comparator_1 (.a(Ctor), .b(\input ), .eq(Cond_Ctor__Input));  // open: gt, lt

  // Other names for the same wires on the sheet: Clear_Registers = CLR; Ctor____input = Cond_Ctor__Input;
  //   L_2__ctor = L_2__t

  // Notes on the sheet:
  //   (2**m)
  //   -1
endmodule

module Mersenne_Control_Unit (
  input  Start,
  input  C____N,
  input  Clock,
  output END,
  output LC,
  output L2_t,
  output [1:0] S2_t,
  output CR
);

  wire d_ff_1_q, d_ff_3_q, d_ff_6_q, d_ff_8_q, demultiplexer_1_out0, L02_t, LC0, LC1, or_1_out, RESET;

  D_Flip_Flop d_ff_1 (.clk(Clock), .D(demultiplexer_1_out0), .Q(d_ff_1_q), .preset(RESET));  // open: Qn, en, reset
  Demultiplexer #(.enable("false")) demultiplexer_1 (
    .out0(demultiplexer_1_out0), .out1(CR), .in(d_ff_1_q), .sel(Start));
  D_Flip_Flop d_ff_2 (.Qn(RESET), .preset(Clock), .reset(d_ff_3_q));  // open: clk, D, Q, en
  D_Flip_Flop d_ff_3 (.clk(Clock), .D(END), .Q(d_ff_3_q));  // open: Qn, preset, en, reset
  D_Flip_Flop d_ff_4 (.clk(Clock), .D(CR), .Q(LC0), .reset(RESET));  // open: Qn, preset, en
  D_Flip_Flop d_ff_5 (.clk(Clock), .D(LC0), .Q(L02_t), .reset(RESET));  // open: Qn, preset, en
  or or_1 (or_1_out, L02_t, d_ff_8_q);
  D_Flip_Flop d_ff_6 (.clk(Clock), .D(or_1_out), .Q(d_ff_6_q), .reset(RESET));  // open: Qn, preset, en
  Demultiplexer #(.enable("false")) demultiplexer_2 (.out0(S2_t[0]), .out1(S2_t[1]), .in(d_ff_6_q), .sel(C____N));
  or or_2 (LC, LC0, LC1);
  or or_3 (L2_t, L02_t, S2_t[0], S2_t[1]);
  D_Flip_Flop d_ff_7 (.clk(Clock), .D(S2_t[0]), .Q(LC1), .reset(RESET));  // open: Qn, preset, en
  D_Flip_Flop d_ff_8 (.clk(Clock), .D(LC1), .Q(d_ff_8_q), .reset(RESET));  // open: Qn, preset, en
  D_Flip_Flop d_ff_9 (.clk(Clock), .D(S2_t[1]), .Q(END), .reset(RESET));  // open: Qn, preset, en

  // Other names for the same wires on the sheet: CLK = Clock; L12_t = S2_t[0]; S01_2_t = S2_t[0]; L22_t = S2_t[1];
  //   S10_2_t = S2_t[1]

  // Notes on the sheet:
  //   IDLE
  //   WHILE
endmodule

module Mersenne_ASM (
  input  [31:0] \input ,
  input  Start,
  input  CLK,
  output [31:0] NumMersenne,
  output END
);

  wire mersenne_control_unit_1_cr, mersenne_control_unit_1_l2_t, mersenne_control_unit_1_lc,
       mersenne_datapath_1_cond_ctor__input;
  wire [1:0] mersenne_control_unit_1_s2_t;

  Mersenne_Control_Unit mersenne_control_unit_1 (
    .Clock(CLK), .END(END), .LC(mersenne_control_unit_1_lc), .L2_t(mersenne_control_unit_1_l2_t),
    .S2_t(mersenne_control_unit_1_s2_t), .Start(Start), .C____N(mersenne_datapath_1_cond_ctor__input),
    .CR(mersenne_control_unit_1_cr));
  Mersenne_DataPath mersenne_datapath_1 (
    .\input (\input ), .CLK(CLK), .L_2__t(mersenne_control_unit_1_l2_t), .L_Ctor(mersenne_control_unit_1_lc),
    .Cond_Ctor__Input(mersenne_datapath_1_cond_ctor__input), .Selector_2__t(mersenne_control_unit_1_s2_t),
    .End(END), .num_mersenne(NumMersenne), .CLR(mersenne_control_unit_1_cr));
  // Probe on NumMersenne

  // Other names for the same wires on the sheet: Num_Mersene[31:0] = NumMersenne
endmodule

module IsPrime_Control_Unit (
  input  Start,
  input  C___N,
  input  N___C____0,
  input  N____2,
  input  Clock,
  output END,
  output LC,
  output SC,
  output LR,
  output CR
);

  wire d_ff_1_q, d_ff_3_q, d_ff_4_q, d_ff_5_q, demultiplexer_1_out0, demultiplexer_2_out1,
       demultiplexer_3_out0, demultiplexer_3_out1, demultiplexer_4_out1, LC0, or_1_out, or_3_out, RESET;

  D_Flip_Flop d_ff_1 (.clk(Clock), .D(demultiplexer_1_out0), .Q(d_ff_1_q), .preset(RESET));  // open: Qn, en, reset
  Demultiplexer #(.enable("false")) demultiplexer_1 (
    .out0(demultiplexer_1_out0), .out1(CR), .in(d_ff_1_q), .sel(Start));
  D_Flip_Flop d_ff_2 (.Qn(RESET), .preset(Clock), .reset(d_ff_3_q));  // open: clk, D, Q, en
  D_Flip_Flop d_ff_3 (.clk(Clock), .D(END), .Q(d_ff_3_q));  // open: Qn, preset, en, reset
  D_Flip_Flop d_ff_4 (.clk(Clock), .D(CR), .Q(d_ff_4_q), .reset(RESET));  // open: Qn, preset, en
  Demultiplexer #(.enable("false")) demultiplexer_2 (
    .out0(LC0), .out1(demultiplexer_2_out1), .in(d_ff_4_q), .sel(N____2));
  or or_1 (or_1_out, LC0, SC);
  D_Flip_Flop d_ff_5 (.clk(Clock), .D(or_1_out), .Q(d_ff_5_q), .reset(RESET));  // open: Qn, preset, en
  Demultiplexer #(.enable("false")) demultiplexer_3 (
    .out0(demultiplexer_3_out0), .out1(demultiplexer_3_out1), .in(d_ff_5_q), .sel(C___N));
  or or_2 (LC, LC0, SC);
  Demultiplexer #(.enable("false")) demultiplexer_4 (
    .out0(SC), .out1(demultiplexer_4_out1), .in(demultiplexer_3_out1), .sel(N___C____0));
  or or_3 (or_3_out, demultiplexer_3_out0, demultiplexer_4_out1, demultiplexer_2_out1);
  D_Flip_Flop d_ff_6 (.clk(Clock), .D(or_3_out), .Q(LR), .reset(RESET));  // open: Qn, preset, en
  D_Flip_Flop d_ff_7 (.clk(Clock), .D(LR), .Q(END), .reset(RESET));  // open: Qn, preset, en

  // Other names for the same wires on the sheet: CLK = Clock; LC1 = SC
endmodule

module IsPrime_DataPath (
  input  [31:0] INPUT,
  input  CLK,
  input  Selector_Ctor,
  input  L_Ctor,
  input  LR,
  input  CLR,
  output RESULT,
  output Ctor_Input,
  output Input_Ctor__0,
  output N____2
);

  wire not_1_out, or_1_out;
  wire [31:0] Ctor, Ctor__1, Input_Ctor, multiplexer_1_out;

  Multiplexer #(.width(32), .enable("false")) multiplexer_1 (
    .in0(32'h2), .in1(Ctor__1), .out(multiplexer_1_out), .sel(Selector_Ctor));
  Adder #(.width(32)) adder_1 (.a(Ctor), .b(32'h1), .out(Ctor__1));  // open: cin, cout
  Divider #(.width(32)) divider_1 (.a(INPUT), .b(Ctor), .rem(Input_Ctor));  // open: out, upper
  Comparator #(.width(32), .mode("unsigned")) comparator_1 (.a(INPUT), .b(32'h2), .eq(N____2));  // open: gt, lt
  Register #(.width(32)) Contador (.D(multiplexer_1_out), .en(L_Ctor), .Q(Ctor), .clk(CLK), .clr(CLR));
  not not_1 (not_1_out, Input_Ctor__0);
  or or_1 (or_1_out, not_1_out, N____2);
  Comparator #(.width(32)) comparator_2 (.a(Ctor__1), .b(INPUT), .lt(Ctor_Input));  // open: gt, eq
  Comparator #(.width(32)) comparator_3 (.a(Input_Ctor), .b({32{1'b0}}), .eq(Input_Ctor__0));  // open: gt, lt
  Register #(.width(1)) u_RESULT (.D(or_1_out), .en(LR), .Q(RESULT), .clk(CLK));  // open: clr

  // Other names for the same wires on the sheet: Clear_Registers = CLR; Input_Ctor____0 = Input_Ctor__0; L_C = L_Ctor
endmodule

module IsPrime_ASM (
  input  [31:0] INPUT,
  input  Start,
  input  CLK,
  output RESULT,
  output END
);

  wire isprime_control_unit_1_cr, isprime_control_unit_1_lc, isprime_control_unit_1_lr,
       isprime_control_unit_1_sc, isprime_datapath_1_ctor_input, isprime_datapath_1_input_ctor__0,
       isprime_datapath_1_n____2;

  // Probe on INPUT
  IsPrime_Control_Unit isprime_control_unit_1 (
    .C___N(isprime_datapath_1_ctor_input), .N___C____0(isprime_datapath_1_input_ctor__0), .Clock(CLK),
    .END(END), .LC(isprime_control_unit_1_lc), .SC(isprime_control_unit_1_sc),
    .LR(isprime_control_unit_1_lr), .Start(Start), .N____2(isprime_datapath_1_n____2),
    .CR(isprime_control_unit_1_cr));
  IsPrime_DataPath isprime_datapath_1 (
    .INPUT(INPUT), .CLK(CLK), .Selector_Ctor(isprime_control_unit_1_sc), .L_Ctor(isprime_control_unit_1_lc),
    .LR(isprime_control_unit_1_lr), .RESULT(RESULT), .Ctor_Input(isprime_datapath_1_ctor_input),
    .Input_Ctor__0(isprime_datapath_1_input_ctor__0), .N____2(isprime_datapath_1_n____2),
    .CLR(isprime_control_unit_1_cr));
endmodule

module PerfectNumber_DataPath (
  input  [31:0] M,
  input  [31:0] Mersenne,
  input  LPN,
  input  LC,
  input  End,
  input  [1:0] SN,
  input  Clock,
  input  CLR,
  output [31:0] Numero_Perfecto,
  output C___M
);

  wire [31:0] _2___m_1, Contador, Contador___1, multiplexer_1_out, num_Perf, numero_perfecto_t;

  Register #(.width(32)) u_CONTADOR (.D(Contador___1), .en(LC), .Q(Contador), .clk(Clock), .clr(CLR));
  Multiplier #(.width(32)) multiplier_1 (.a(num_Perf), .b(32'h2), .out(_2___m_1));  // open: cin, cout
  Multiplier #(.width(32)) multiplier_2 (.a(num_Perf), .b(Mersenne), .out(numero_perfecto_t));  // open: cin, cout
  Adder #(.width(32)) adder_1 (.a(Contador), .b(32'h1), .out(Contador___1));  // open: cin, cout
  Comparator #(.width(32)) comparator_1 (.a(Contador), .b(M), .lt(C___M));  // open: gt, eq
  Multiplexer #(.select(2), .width(32), .enable("false")) multiplexer_1 (
    .in0(32'h1), .in1(_2___m_1), .in2(numero_perfecto_t), .out(multiplexer_1_out), .sel(SN));  // open: in3
  Register #(.width(32)) u_Numero_Perfecto (.D(num_Perf), .en(End), .Q(Numero_Perfecto), .clk(Clock));  // open: clr
  Register #(.width(32)) Numero_Perfecto_2 (.D(multiplexer_1_out), .en(LPN), .Q(num_Perf), .clk(Clock), .clr(CLR));

  // Other names for the same wires on the sheet: Clear_Register = CLR; CLK = Clock; input[31:0] = M; L_contador = LC;
  //   L_numPerf = LPN; Selector_de_2__m_1[1:0] = SN

  // Notes on the sheet:
  //   2**(m-1) * 2**m -1
endmodule

module PerfectNumber_Control_Unit (
  input  C___M,
  input  Start,
  input  Clock,
  input  [31:0] Pow,
  output END,
  output LPN,
  output LC,
  output [1:0] SN,
  output [31:0] Mersenne,
  output CLR
);

  wire d_ff_1_q, d_ff_3_q, d_ff_6_q, demultiplexer_1_out0, demultiplexer_2_out0, LC0, LC1, LPN0,
       mersenne_asm_1_end, or_1_out, RESET;

  Demultiplexer #(.enable("false")) demultiplexer_1 (
    .out0(demultiplexer_1_out0), .out1(CLR), .in(d_ff_1_q), .sel(Start));
  D_Flip_Flop d_ff_1 (.clk(Clock), .D(demultiplexer_1_out0), .Q(d_ff_1_q), .preset(RESET));  // open: Qn, en, reset
  D_Flip_Flop d_ff_2 (.Qn(RESET), .preset(Clock), .reset(d_ff_3_q));  // open: clk, D, Q, en
  D_Flip_Flop d_ff_3 (.clk(Clock), .D(END), .Q(d_ff_3_q));  // open: Qn, preset, en, reset
  D_Flip_Flop d_ff_4 (.clk(Clock), .D(CLR), .Q(LPN0), .reset(RESET));  // open: Qn, preset, en
  D_Flip_Flop d_ff_5 (.clk(Clock), .D(LPN0), .Q(LC0), .reset(RESET));  // open: Qn, preset, en
  or or_1 (or_1_out, LC0, LC1);
  D_Flip_Flop d_ff_6 (.clk(Clock), .D(or_1_out), .Q(d_ff_6_q), .reset(RESET));  // open: Qn, preset, en
  Demultiplexer #(.enable("false")) demultiplexer_2 (
    .out0(demultiplexer_2_out0), .out1(SN[0]), .in(d_ff_6_q), .sel(C___M));
  or or_2 (LPN, LPN0, SN[0], SN[1]);
  or or_3 (LC, LC0, LC1);
  Mersenne_ASM mersenne_asm_1 (
    .\input (Pow), .NumMersenne(Mersenne), .Start(demultiplexer_2_out0), .END(mersenne_asm_1_end), .CLK(Clock));
  D_Flip_Flop d_ff_7 (.clk(Clock), .D(SN[0]), .Q(LC1), .reset(RESET));  // open: Qn, preset, en
  D_Flip_Flop d_ff_8 (.clk(Clock), .D(mersenne_asm_1_end), .Q(SN[1]), .reset(RESET));  // open: Qn, preset, en
  D_Flip_Flop d_ff_9 (.clk(Clock), .D(SN[1]), .Q(END), .reset(RESET));  // open: Qn, preset, en

  // Other names for the same wires on the sheet: CLK = Clock; COUNTER___M = C___M; input[31:0] = Pow; LPN1 = SN[0];
  //   SN01 = SN[0]; LPN2 = SN[1]; SN10 = SN[1]
endmodule

module Perfect_Number_ASM (
  input  Start,
  input  [31:0] Input,
  input  in_3,
  output [31:0] Perfect_Number,
  output END
);

  wire perfectnumber_control_unit_1_clr, perfectnumber_control_unit_1_lc, perfectnumber_control_unit_1_lpn,
       perfectnumber_datapath_1_c___m;
  wire [1:0] perfectnumber_control_unit_1_sn;
  wire [31:0] perfectnumber_control_unit_1_mersenne;

  PerfectNumber_Control_Unit perfectnumber_control_unit_1 (
    .C___M(perfectnumber_datapath_1_c___m), .Start(Start), .Clock(in_3), .Pow(Input), .END(END),
    .LPN(perfectnumber_control_unit_1_lpn), .LC(perfectnumber_control_unit_1_lc),
    .SN(perfectnumber_control_unit_1_sn), .Mersenne(perfectnumber_control_unit_1_mersenne),
    .CLR(perfectnumber_control_unit_1_clr));
  PerfectNumber_DataPath perfectnumber_datapath_1 (
    .M(Input), .LPN(perfectnumber_control_unit_1_lpn), .LC(perfectnumber_control_unit_1_lc), .Clock(in_3),
    .SN(perfectnumber_control_unit_1_sn), .Numero_Perfecto(Perfect_Number),
    .C___M(perfectnumber_datapath_1_c___m), .Mersenne(perfectnumber_control_unit_1_mersenne), .End(END),
    .CLR(perfectnumber_control_unit_1_clr));
  // Probe on Perfect_Number

  // Other names for the same wires on the sheet: CLK = in_3
endmodule

module Nth_Perfect_Number_DataPath (
  input  [31:0] Perfect_Number,
  input  L_M,
  input  Selector_M,
  input  L_Contador,
  input  END,
  input  CLK,
  input  CLR,
  input  [31:0] INPUT,
  input  LIN,
  output Contador__Input,
  output [31:0] M,
  output [31:0] Result
);

  wire undriven;
  wire [31:0] Contador, Contador_1, input_t, M_1, multiplexer_1_out;

  Register #(.width(32)) register_1 (.D(INPUT), .en(LIN), .Q(input_t), .clk(CLK), .clr(undriven));
  Multiplexer #(.width(32), .enable("false")) multiplexer_1 (
    .in0(32'h2), .in1(M_1), .out(multiplexer_1_out), .sel(Selector_M));
  Register #(.width(32)) u_Contador (.D(Contador_1), .en(L_Contador), .Q(Contador), .clk(CLK), .clr(CLR));
  Register #(.width(32)) register_2 (.D(Perfect_Number), .en(END), .Q(Result), .clk(CLK));  // open: clr
  Register #(.width(32)) u_M (.D(multiplexer_1_out), .en(L_M), .Q(M), .clk(CLK), .clr(CLR));
  Adder #(.width(32)) adder_1 (.a(Contador), .b(32'h1), .out(Contador_1));  // open: cin, cout
  Adder #(.width(32)) adder_2 (.a(M), .b(32'h1), .out(M_1));  // open: cin, cout
  Comparator #(.width(32), .mode("unsigned")) comparator_1 (
    .a(Contador), .b(input_t), .lt(Contador__Input));  // open: gt, eq

  // Other names for the same wires on the sheet: IN[31:0] = INPUT; L_Ctor = L_Contador;
  //   Numero_Perfecto[31:0] = Perfect_Number; Resultado[31:0] = Result; S_M = Selector_M
endmodule

module Nth_PerfectNumber_Control_Unit (
  input  [31:0] M,
  input  Contador___Input,
  input  Clock,
  output END,
  output [31:0] Perfect_Number,
  output LM,
  output SM,
  output LC,
  output CLR,
  output LIN
);

  wire d_ff_1_q, d_ff_5_q, d_ff_6_q, d_ff_7_q, d_ff_8_q, d_ff_10_q, d_ff_12_q, demultiplexer_1_out0,
       demultiplexer_2_out0, demultiplexer_2_out1, demultiplexer_3_out0, demultiplexer_3_out1, END_MERSENNE,
       isprime_asm_1_end, isprime_asm_2_end, IsPrime_m, IsPrime_m____IsPrime_Mersenne, IsPrime_Mersenne, LM0,
       mersenne_asm_1_end, or_1_out, perfect_number_asm_1_end, RESET, START;
  wire [31:0] NumMersenne;

  D_Flip_Flop d_ff_1 (.clk(Clock), .D(demultiplexer_1_out0), .Q(d_ff_1_q), .preset(RESET));  // open: Qn, en, reset
  Demultiplexer demultiplexer_1 (.out0(demultiplexer_1_out0), .out1(CLR), .in(d_ff_1_q), .sel(START));  // open: en
  D_Flip_Flop d_ff_2 (.Q(START), .Qn(RESET), .preset(Clock));  // open: clk, D, en, reset
  IsPrime_ASM isprime_asm_1 (.INPUT(M), .RESULT(IsPrime_m), .END(isprime_asm_1_end), .Start(END_MERSENNE), .CLK(Clock));
  D_Flip_Flop d_ff_3 (.clk(Clock), .D(CLR), .Q(LIN), .reset(RESET));  // open: Qn, preset, en
  D_Flip_Flop d_ff_4 (.clk(Clock), .D(LIN), .Q(LM0), .reset(RESET));  // open: Qn, preset, en
  D_Flip_Flop d_ff_5 (.clk(Clock), .D(isprime_asm_1_end), .Q(d_ff_5_q), .reset(RESET));  // open: Qn, preset, en
  IsPrime_ASM isprime_asm_2 (
    .INPUT(NumMersenne), .RESULT(IsPrime_Mersenne), .END(isprime_asm_2_end), .Start(d_ff_5_q), .CLK(Clock));
  D_Flip_Flop d_ff_6 (.clk(Clock), .D(LM0), .Q(d_ff_6_q), .reset(RESET));  // open: Qn, preset, en
  or or_1 (or_1_out, d_ff_6_q, SM);
  D_Flip_Flop d_ff_7 (.clk(Clock), .D(isprime_asm_2_end), .Q(d_ff_7_q), .reset(RESET));  // open: Qn, preset, en
  // Probe on IsPrime_m
  and and_1 (IsPrime_m____IsPrime_Mersenne, IsPrime_m, IsPrime_Mersenne);
  // Probe on IsPrime_Mersenne
  Demultiplexer demultiplexer_2 (
    .out0(demultiplexer_2_out0), .out1(demultiplexer_2_out1), .in(d_ff_8_q), .sel(Contador___Input));  // open: en
  D_Flip_Flop d_ff_8 (.clk(Clock), .D(or_1_out), .Q(d_ff_8_q), .reset(RESET));  // open: Qn, preset, en
  Demultiplexer #(.enable("false")) demultiplexer_3 (
    .out0(demultiplexer_3_out0), .out1(demultiplexer_3_out1), .in(d_ff_7_q),
    .sel(IsPrime_m____IsPrime_Mersenne));
  Mersenne_ASM mersenne_asm_1 (
    .\input (M), .NumMersenne(NumMersenne), .Start(demultiplexer_2_out1), .END(mersenne_asm_1_end),
    .CLK(Clock));
  Perfect_Number_ASM perfect_number_asm_1 (
    .Input(M), .Perfect_Number(Perfect_Number), .Start(demultiplexer_3_out1), .END(perfect_number_asm_1_end),
    .in_3(Clock));
  // Probe on NumMersenne
  D_Flip_Flop d_ff_9 (.clk(Clock), .D(mersenne_asm_1_end), .Q(END_MERSENNE), .reset(RESET));  // open: Qn, preset, en
  D_Flip_Flop d_ff_10 (
    .clk(Clock), .D(perfect_number_asm_1_end), .Q(d_ff_10_q), .reset(RESET));  // open: Qn, preset, en
  D_Flip_Flop d_ff_11 (.clk(Clock), .D(d_ff_10_q), .Q(LC), .reset(RESET));  // open: Qn, preset, en
  // Probe on Perfect_Number
  or or_2 (LM, LM0, SM);
  D_Flip_Flop d_ff_12 (.clk(Clock), .D(LC), .Q(d_ff_12_q), .reset(RESET));  // open: Qn, preset, en
  or or_3 (SM, demultiplexer_3_out0, d_ff_12_q);
  D_Flip_Flop d_ff_13 (.clk(Clock), .D(demultiplexer_2_out0), .Q(END), .reset(RESET));  // open: Qn, preset, en

  // Other names for the same wires on the sheet: C___N = Contador___Input; CLK = Clock; LM1 = SM
endmodule
