// Logisim project BigASM.circ as structural Verilog
module BOARD_BIG_ASM (
  output out_1
);

  wire button_1_out, CLK, CLR, d_ff_1_q, not_1_out, Write, Write_ASCII;
  wire [6:0] ASCII;
  wire [7:0] counter_1_q;
  wire [23:0] Dir_INPUT, Dir_MEMORY;
  wire [31:0] INPUT, MEMORY_IN, MEMORY_OUT;

  Button button_1 (.out(button_1_out));
  Clock clock_1 (.out(CLK));
  D_Flip_Flop d_ff_1 (.clk(CLK), .D(1'b1), .Q(d_ff_1_q), .reset(button_1_out));  // open: Qn, preset, en
  D_Flip_Flop d_ff_2 (.clk(CLK), .D(d_ff_1_q), .Qn(CLR), .reset(button_1_out));  // open: Q, preset, en
  BIG_ASM big_asm_1 (
    .DATA_INPUT(INPUT), .MEMORY_IN(MEMORY_OUT), .CLK(CLK), .CLR(CLR), .DIR_INPUT(Dir_INPUT),
    .MEMORY_OUT(MEMORY_IN), .DIR_MEMORY(Dir_MEMORY), .Write_OUTPUT(Write), .ASCII(ASCII),
    .Write_ASCII(Write_ASCII), .END(out_1));
  MEMORY memory_1 (.DIR(Dir_MEMORY), .DATA_IN(MEMORY_IN), .WRITE(Write), .CLK(CLK), .CLR(CLR), .DATA_OUT(MEMORY_OUT));
  INPUT input_1 (.DIR(Dir_INPUT), .CLK(CLK), .DATA_OUT(INPUT));
  Counter counter_1 (.load(1'b0), .count(not_1_out), .Q(counter_1_q), .clk(CLK), .clr(CLR));  // open: D, carry
  not not_1 (not_1_out, out_1);
  // Probe on counter_1_q
  TTY #(.rows(32), .cols(60)) tty_1 (.data(ASCII), .clk(CLK), .we(Write_ASCII), .clr(CLR));

  // Other names for the same wires on the sheet: END = out_1

  // Notes on the sheet:
  //   COUNTER
  //   BOARD
endmodule

module INPUT (
  input  [23:0] DIR,
  input  CLK,
  output [31:0] DATA_OUT
);

  RAM #(.addrWidth(24), .dataWidth(32)) ram_1 (.addr(DIR), .data(DATA_OUT), .clk(CLK), .ld(1'b1));  // open: sel, clr
endmodule

module MEMORY (
  input  [23:0] DIR,
  input  [31:0] DATA_IN,
  input  WRITE,
  input  CLK,
  input  CLR,
  output [31:0] DATA_OUT
);

  RAM #(.addrWidth(24), .dataWidth(32), .bus("separate")) ram_1 (
    .addr(DIR), .din(DATA_IN), .data(DATA_OUT), .str(WRITE), .clk(CLK), .clr(CLR));  // open: sel, ld
endmodule

module BIG_ASM (
  input  [31:0] DATA_INPUT,
  input  [31:0] MEMORY_IN,
  input  CLK,
  input  CLR,
  output [23:0] DIR_INPUT,
  output [31:0] MEMORY_OUT,
  output [23:0] DIR_MEMORY,
  output Write_OUTPUT,
  output [6:0] ASCII,
  output Write_ASCII,
  output END
);

  wire AI____AJ, I___N___1, J___N, LAI, LAJ, LI, LMA, LN, LR, LX, MATCH, PRINT, printer_1_li, printer_1_lj,
       printer_1_ln, SI, SMA;
  wire [23:0] data_path_1_i, data_path_1_n;
  wire [31:0] printer_dp_1_io, printer_dp_1_jo, printer_dp_1_no;

  CONTROL_UNIT control_unit_1 (
    .CLK(CLK), .CLR(CLR), .I___N___1(I___N___1), .J___N(J___N), .AI____AJ(AI____AJ), .END(PRINT), .LX(LX),
    .LN(LN), .LMA(LMA), .SMA(SMA), .LI(LI), .SI(SI), .LAI(LAI), .LAJ(LAJ), .LR(LR));
  PRINTER printer_1 (
    .CLK(CLK), .MATCH(MATCH), .N___1(printer_dp_1_no), .I(printer_dp_1_io), .J(printer_dp_1_jo), .END(END),
    .LN(printer_1_ln), .LI(printer_1_li), .LJ(printer_1_lj), .START(PRINT), .CLR(CLR), .ASCII(ASCII),
    .WASCII(Write_ASCII));
  PRINTER_DP printer_dp_1 (
    .N___1(data_path_1_n), .I(data_path_1_i), .J(DIR_INPUT), .CLK(CLK), .CLR(CLR), .LN(printer_1_ln),
    .LI(printer_1_li), .LJ(printer_1_lj), .NO(printer_dp_1_no), .IO(printer_dp_1_io), .JO(printer_dp_1_jo));
  DATA_PATH data_path_1 (
    .LX(LX), .SMA(SMA), .LMA(LMA), .SI(SI), .LN(LN), .LI(LI), .INPUT(DATA_INPUT), .LAi(LAI), .LAj(LAJ),
    .LR(LR), .CLK(CLK), .CLR(CLR), .AI___AJ____X(AI____AJ), .MEMORY_ADDRESS(DIR_INPUT),
    .I___N___1(I___N___1), .J___N(J___N), .MATCH(MATCH), .I(data_path_1_i), .N(data_path_1_n));

  // Other names for the same wires on the sheet: INPUT[31:0] = DATA_INPUT; MA[23:0] = DIR_INPUT; WASCII = Write_ASCII
endmodule

module PRINT_UDEC (
  input  [31:0] num,
  input  start,
  input  CLK,
  input  RST,
  output [6:0] ASCII,
  output Write_ASCII,
  output \end 
);

  wire _0_c, _0_n, demultiplexer_1_out0, demultiplexer_2_out0, demultiplexer_2_out1, demultiplexer_3_out0,
       demultiplexer_3_out1, IDLE_2_q, IDLE_3_q, IDLE_4_q, IDLE_q, Lc, Lc_0, Ln, Ln_0, or_1_out;
  wire [23:0] bit_extender_1_out;
  wire [31:0] c, c___1, c___1_t, divider_1_rem, memory_1_data_out, multiplexer_1_out, multiplexer_2_out,
       multiplexer_3_out, n, n___10, n___10___48;

  Multiplexer #(.width(32), .enable("false")) multiplexer_1 (
    .in0(num), .in1(n___10), .out(multiplexer_1_out), .sel(Lc_0));
  Divider #(.width(32)) divider_1 (.a(n), .b(32'ha), .out(n___10), .rem(divider_1_rem));  // open: upper
  Adder #(.width(32)) adder_1 (.a(divider_1_rem), .b(32'h30), .out(n___10___48));  // open: cin, cout
  or or_1 (or_1_out, demultiplexer_1_out0, \end );
  Register #(.width(32)) u_n (.D(multiplexer_1_out), .en(Ln), .Q(n), .clk(CLK), .clr(RST));
  D_Flip_Flop IDLE (.clk(CLK), .D(or_1_out), .Q(IDLE_q), .preset(RST));  // open: Qn, en, reset
  Demultiplexer #(.enable("false")) demultiplexer_1 (
    .out0(demultiplexer_1_out0), .out1(Ln_0), .in(IDLE_q), .sel(start));
  or or_2 (Write_ASCII, demultiplexer_3_out0, demultiplexer_2_out1);
  Multiplexer #(.width(32), .enable("false")) multiplexer_2 (
    .in0(c___1), .in1(c___1_t), .out(multiplexer_2_out), .sel(Write_ASCII));
  Adder #(.width(32)) adder_2 (.a(c), .b(32'h1), .out(c___1));  // open: cin, cout
  Subtractor #(.width(32)) subtractor_1 (.a(c), .b(32'h1), .out(c___1_t));  // open: bin, bout
  D_Flip_Flop IDLE_2 (.clk(CLK), .D(Ln_0), .Q(IDLE_2_q), .reset(RST));  // open: Qn, preset, en
  Register #(.width(32)) u_c (.D(multiplexer_2_out), .en(Lc), .Q(c), .clk(CLK), .clr(RST));
  or or_3 (Lc_0, IDLE_2_q, demultiplexer_3_out1);
  Multiplexer #(.width(32), .enable("false")) multiplexer_3 (
    .in0(c), .in1(c___1_t), .out(multiplexer_3_out), .sel(Write_ASCII));
  Comparator #(.width(32), .mode("unsigned")) comparator_1 (.a({32{1'b0}}), .b(n), .lt(_0_n));  // open: gt, eq
  Comparator #(.width(32), .mode("unsigned")) comparator_2 (.a({32{1'b0}}), .b(c), .lt(_0_c));  // open: gt, eq
  D_Flip_Flop IDLE_3 (.clk(CLK), .D(Write_ASCII), .Q(IDLE_3_q), .reset(RST));  // open: Qn, preset, en
  Demultiplexer #(.enable("false")) demultiplexer_2 (
    .out0(demultiplexer_2_out0), .out1(demultiplexer_2_out1), .in(IDLE_3_q), .sel(_0_c));
  Bit_Extender #(.in_width(32), .out_width(24)) bit_extender_1 (.in(multiplexer_3_out), .out(bit_extender_1_out));
  D_Flip_Flop IDLE_4 (.clk(CLK), .D(Lc_0), .Q(IDLE_4_q), .reset(RST));  // open: Qn, preset, en
  or or_4 (Lc, Lc_0, Write_ASCII);
  or or_5 (Ln, Ln_0, Lc_0);
  Demultiplexer #(.enable("false")) demultiplexer_3 (
    .out0(demultiplexer_3_out0), .out1(demultiplexer_3_out1), .in(IDLE_4_q), .sel(_0_n));
  D_Flip_Flop IDLE_5 (.clk(CLK), .D(demultiplexer_2_out0), .Q(\end ), .reset(RST));  // open: Qn, preset, en
  MEMORY memory_1 (
    .DIR(bit_extender_1_out), .DATA_IN(n___10___48), .WRITE(Lc_0), .CLK(CLK), .CLR(RST),
    .DATA_OUT(memory_1_data_out));
  Bit_Extender #(.in_width(32), .out_width(7)) bit_extender_2 (.in(memory_1_data_out), .out(ASCII));

  // Other names for the same wires on the sheet: Lc_1 = Write_ASCII; Sc = Write_ASCII; Ln_1 = Lc_0; Sn = Lc_0;
  //   Write = Lc_0
endmodule

module PRINT_DEC (
  input  [31:0] num,
  input  start,
  input  CLK,
  input  RST,
  output [6:0] ASCII,
  output Write_ASCII,
  output END
);

  wire demultiplexer_1_out0, demultiplexer_1_out1, demultiplexer_2_out0, demultiplexer_3_out0, end_t,
       IDLE_3_q, IDLE_q, or_1_out, or_2_out, or_3_out, S_ASCII, startUDEC, Write_ASCII_1;
  wire [6:0] ASCII_t;
  wire [31:0] multiplexer_1_out, negator_1_out;

  or or_1 (or_1_out, demultiplexer_1_out0, END);
  Negator #(.width(32)) negator_1 (.in(num), .out(negator_1_out));
  D_Flip_Flop IDLE (.clk(CLK), .D(or_1_out), .Q(IDLE_q), .preset(RST));  // open: Qn, en, reset
  Demultiplexer #(.enable("false")) demultiplexer_1 (
    .out0(demultiplexer_1_out0), .out1(demultiplexer_1_out1), .in(IDLE_q), .sel(start));
  Multiplexer #(.width(32), .enable("false")) multiplexer_1 (
    .in0(num), .in1(negator_1_out), .out(multiplexer_1_out), .sel(num[31]));
  Demultiplexer #(.enable("false")) demultiplexer_2 (
    .out0(demultiplexer_2_out0), .out1(S_ASCII), .in(demultiplexer_1_out1), .sel(num[31]));
  or or_2 (or_2_out, demultiplexer_2_out0, S_ASCII);
  D_Flip_Flop IDLE_2 (.clk(CLK), .D(or_2_out), .Q(startUDEC), .reset(RST));  // open: Qn, preset, en
  PRINT_UDEC print_udec_1 (
    .num(multiplexer_1_out), .start(startUDEC), .CLK(CLK), .RST(RST), .ASCII(ASCII_t),
    .Write_ASCII(Write_ASCII_1), .\end (end_t));
  D_Flip_Flop IDLE_3 (.clk(CLK), .D(or_3_out), .Q(IDLE_3_q), .reset(RST));  // open: Qn, preset, en
  or or_3 (or_3_out, startUDEC, demultiplexer_3_out0);
  Demultiplexer #(.enable("false")) demultiplexer_3 (
    .out0(demultiplexer_3_out0), .out1(END), .in(IDLE_3_q), .sel(end_t));
  Multiplexer #(.width(7), .enable("false")) multiplexer_2 (
    .in0(ASCII_t), .in1(7'b0101101), .out(ASCII), .sel(S_ASCII));
  or or_4 (Write_ASCII, S_ASCII, Write_ASCII_1);

  // Other names for the same wires on the sheet: sign = num[31]; Write_ASCII_0 = S_ASCII
endmodule

module TEST_PRINT (
  input  [31:0] in_1,
  output out_2
);

  wire button_1_out, button_2_out, CLK, CLR, d_ff_1_q, Write_ASCII;
  wire [6:0] ASCII;

  Button button_1 (.out(button_1_out));
  Clock clock_1 (.out(CLK));
  D_Flip_Flop d_ff_1 (.clk(CLK), .D(1'b1), .Q(d_ff_1_q), .reset(button_1_out));  // open: Qn, preset, en
  D_Flip_Flop d_ff_2 (.clk(CLK), .D(d_ff_1_q), .Qn(CLR), .reset(button_1_out));  // open: Q, preset, en
  Button button_2 (.out(button_2_out));
  PRINT_UDEC print_udec_1 ();  // open: num, start, CLK, RST, ASCII, Write_ASCII, end
  PRINT_DEC print_dec_1 (
    .num(in_1), .start(button_2_out), .CLK(CLK), .RST(CLR), .ASCII(ASCII), .Write_ASCII(Write_ASCII),
    .END(out_2));
  TTY #(.rows(32), .cols(60)) tty_1 (.data(ASCII), .clk(CLK), .we(Write_ASCII), .clr(CLR));
endmodule

module DATA_PATH (
  input  LX,
  input  SMA,
  input  LMA,
  input  SI,
  input  LN,
  input  LI,
  input  [31:0] INPUT,
  input  LAi,
  input  LAj,
  input  LR,
  input  CLK,
  input  CLR,
  output AI___AJ____X,
  output MATCH,
  output [23:0] MEMORY_ADDRESS,
  output [23:0] I,
  output I___N___1,
  output J___N,
  output [23:0] N
);

  wire [23:0] I___1, MA___1, multiplexer_1_out, multiplexer_2_out, N___2;
  wire [31:0] adder_5_out, AI, AJ, N_t, X;

  // Probe on X
  Register #(.width(32)) u_X (.D(INPUT), .en(LX), .Q(X), .clk(CLK), .clr(CLR));
  Register #(.width(32)) u_AI (.D(INPUT), .en(LAi), .Q(AI), .clk(CLK), .clr(CLR));
  Adder #(.width(24)) adder_1 (.a(MEMORY_ADDRESS), .b(24'h1), .out(MA___1));  // open: cin, cout
  Adder #(.width(24)) adder_2 (.a(I), .b(24'h1), .out(I___1));  // open: cin, cout
  Multiplexer #(.width(24), .enable("false")) multiplexer_1 (
    .in0(MEMORY_ADDRESS), .in1(I___1), .out(multiplexer_1_out), .sel(SI));
  Register #(.width(32)) u_N (.D(INPUT), .en(LN), .Q(N_t), .clk(CLK), .clr(CLR));
  Register #(.width(24)) u_I (.D(multiplexer_1_out), .en(LI), .Q(I), .clk(CLK), .clr(CLR));
  Register #(.width(32)) u_AJ (.D(INPUT), .en(LAj), .Q(AJ), .clk(CLK), .clr(CLR));
  Adder #(.width(24)) adder_3 (.a(N_t[23:0]), .b(24'h1), .out(N));  // open: cin, cout
  Adder #(.width(24)) adder_4 (.a(N_t[23:0]), .b(24'h2), .out(N___2));  // open: cin, cout
  Multiplexer #(.width(24), .enable("false")) multiplexer_2 (.in0(MA___1), .in1(I), .out(multiplexer_2_out), .sel(SMA));
  Register #(.width(24)) MA (.D(multiplexer_2_out), .en(LMA), .Q(MEMORY_ADDRESS), .clk(CLK), .clr(CLR));
  Comparator #(.width(24), .mode("unsigned")) comparator_1 (.a(I), .b(N), .lt(I___N___1));  // open: gt, eq
  Comparator #(.width(24), .mode("unsigned")) comparator_2 (.a(MEMORY_ADDRESS), .b(N___2), .lt(J___N));  // open: gt, eq
  Register #(.width(1)) register_1 (.D(1'b1), .en(LR), .Q(MATCH), .clk(CLK), .clr(CLR));
  // Probe on adder_5_out
  Adder #(.width(32)) adder_5 (.a(AI), .b(AJ), .out(adder_5_out));  // open: cin, cout
  Comparator #(.width(32), .mode("unsigned")) comparator_3 (.a(adder_5_out), .b(X), .eq(AI___AJ____X));  // open: gt, lt
  // Probe on X

  // Other names for the same wires on the sheet: MA[23:0] = MEMORY_ADDRESS; N___1[23:0] = N
endmodule

module CONTROL_UNIT (
  input  CLK,
  input  CLR,
  input  I___N___1,
  input  J___N,
  input  AI____AJ,
  output END,
  output LX,
  output LN,
  output LMA,
  output SMA,
  output LI,
  output SI,
  output LAI,
  output LAJ,
  output LR
);

  wire CONT1, d_ff_1_q, d_ff_8_q, d_ff_9_q, d_ff_10_q, d_ff_12_q, d_ff_13_q, demultiplexer_1_out0,
       demultiplexer_4_out0, LI0, LMA0, LMA1, LMA2, or_1_out, or_4_out, RESET, START;

  D_Flip_Flop d_ff_1 (.clk(CLK), .D(demultiplexer_1_out0), .Q(d_ff_1_q), .preset(RESET));  // open: Qn, en, reset
  Demultiplexer #(.enable("false")) demultiplexer_1 (
    .out0(demultiplexer_1_out0), .out1(LX), .in(d_ff_1_q), .sel(START));
  D_Flip_Flop d_ff_2 (.Q(START), .Qn(RESET), .preset(CLK), .reset(CLR));  // open: clk, D, en
  or or_1 (or_1_out, CONT1, LR);
  D_Flip_Flop d_ff_3 (.clk(CLK), .D(LX), .Q(LMA0), .reset(RESET));  // open: Qn, preset, en
  D_Flip_Flop d_ff_4 (.clk(CLK), .D(or_1_out), .Q(END), .reset(RESET));  // open: Qn, preset, en
  D_Flip_Flop d_ff_5 (.clk(CLK), .D(LMA0), .Q(LN), .reset(RESET));  // open: Qn, preset, en
  or or_2 (LI, LI0, SI);
  D_Flip_Flop d_ff_6 (.clk(CLK), .D(LN), .Q(LMA1), .reset(RESET));  // open: Qn, preset, en
  or or_3 (LMA, LMA0, LMA1, LMA2, SMA);
  D_Flip_Flop d_ff_7 (.clk(CLK), .D(LMA1), .Q(LI0), .reset(RESET));  // open: Qn, preset, en
  D_Flip_Flop d_ff_8 (.clk(CLK), .D(LI0), .Q(d_ff_8_q), .reset(RESET));  // open: Qn, preset, en
  Demultiplexer #(.enable("false")) demultiplexer_2 (.out0(CONT1), .out1(LAI), .in(or_4_out), .sel(I___N___1));
  or or_4 (or_4_out, d_ff_13_q, d_ff_8_q);
  D_Flip_Flop d_ff_9 (.clk(CLK), .D(LAI), .Q(d_ff_9_q), .reset(RESET));  // open: Qn, preset, en
  or or_5 (LMA2, d_ff_9_q, demultiplexer_4_out0);
  D_Flip_Flop d_ff_10 (.clk(CLK), .D(LMA2), .Q(d_ff_10_q), .reset(RESET));  // open: Qn, preset, en
  Demultiplexer #(.enable("false")) demultiplexer_3 (.out0(SI), .out1(LAJ), .in(d_ff_10_q), .sel(J___N));
  D_Flip_Flop d_ff_11 (.clk(CLK), .D(SI), .Q(SMA), .reset(RESET));  // open: Qn, preset, en
  D_Flip_Flop d_ff_12 (.clk(CLK), .D(LAJ), .Q(d_ff_12_q), .reset(RESET));  // open: Qn, preset, en
  Demultiplexer #(.enable("false")) demultiplexer_4 (
    .out0(demultiplexer_4_out0), .out1(LR), .in(d_ff_12_q), .sel(AI____AJ));
  D_Flip_Flop d_ff_13 (.clk(CLK), .D(SMA), .Q(d_ff_13_q), .reset(RESET));  // open: Qn, preset, en

  // Other names for the same wires on the sheet: CONT2 = LR; LI1 = SI; SI1 = SI; LMA3 = SMA; SMA1 = SMA
endmodule

module PRINTER_DP (
  input  [23:0] N___1,
  input  [23:0] I,
  input  [23:0] J,
  input  CLK,
  input  CLR,
  input  LN,
  input  LI,
  input  LJ,
  output [31:0] NO,
  output [31:0] IO,
  output [31:0] JO
);

  wire [23:0] subtractor_1_out, subtractor_2_out;

  Subtractor #(.width(24)) subtractor_1 (.a(I), .b(24'h2), .out(subtractor_1_out));  // open: bin, bout
  Register #(.width(32)) u_N___1 (.D({{8{1'b0}}, N___1}), .en(LN), .Q(NO), .clk(CLK), .clr(CLR));
  Subtractor #(.width(24)) subtractor_2 (.a(J), .b(24'h2), .out(subtractor_2_out));  // open: bin, bout
  Register #(.width(32)) u_I (.D({{8{1'b0}}, subtractor_1_out}), .en(LI), .Q(IO), .clk(CLK), .clr(CLR));
  Register #(.width(32)) u_J (.D({{8{1'b0}}, subtractor_2_out}), .en(LJ), .Q(JO), .clk(CLK), .clr(CLR));
endmodule

module PRINTER (
  input  CLK,
  input  MATCH,
  input  [31:0] N___1,
  input  [31:0] I,
  input  [31:0] J,
  input  START,
  input  CLR,
  output END,
  output [6:0] ASCII,
  output WASCII,
  output LN,
  output LI,
  output LJ
);

  wire d_ff_1_q, d_ff_4_q, d_ff_6_q, demultiplexer_1_out0, demultiplexer_1_out1, demultiplexer_2_out0,
       demultiplexer_2_out1, or_4_out, print_dec_1_end, print_dec_2_end, print_dec_3_end, RESET, WASCII1,
       WASCII2, WASCII3, WASCII4;
  wire [1:0] or_2_out;
  wire [6:0] ASCII1, ASCII2, ASCII4;

  D_Flip_Flop d_ff_1 (.clk(CLK), .D(demultiplexer_1_out0), .Q(d_ff_1_q), .preset(RESET));  // open: Qn, en, reset
  D_Flip_Flop d_ff_2 (.Qn(RESET), .preset(CLK), .reset(CLR));  // open: clk, D, Q, en
  Demultiplexer #(.enable("false")) demultiplexer_1 (
    .out0(demultiplexer_1_out0), .out1(demultiplexer_1_out1), .in(d_ff_1_q), .sel(START));
  D_Flip_Flop d_ff_3 (.clk(CLK), .D(demultiplexer_1_out1), .Q(LI), .reset(RESET));  // open: Qn, preset, en
  D_Flip_Flop d_ff_4 (.clk(CLK), .D(LI), .Q(d_ff_4_q), .reset(RESET));  // open: Qn, preset, en
  Demultiplexer #(.enable("false")) demultiplexer_2 (
    .out0(demultiplexer_2_out0), .out1(demultiplexer_2_out1), .in(d_ff_4_q), .sel(MATCH));
  or or_1 (or_2_out[1], WASCII3, WASCII4);
  Multiplexer #(.select(2), .width(7), .enable("false")) multiplexer_1 (
    .in0(ASCII1), .in1(ASCII2), .in2(7'b0100000), .in3(ASCII4), .out(ASCII), .sel(or_2_out));
  or or_2 (or_2_out[0], WASCII4, WASCII2);
  or or_3 (WASCII, WASCII1, WASCII2, WASCII3, WASCII4);
  PRINT_DEC print_dec_1 (
    .num(I), .start(demultiplexer_2_out1), .CLK(CLK), .RST(RESET), .ASCII(ASCII2), .Write_ASCII(WASCII2),
    .END(print_dec_1_end));
  PRINT_DEC print_dec_2 (
    .num(N___1), .start(demultiplexer_2_out0), .CLK(CLK), .RST(RESET), .ASCII(ASCII1), .Write_ASCII(WASCII1),
    .END(print_dec_2_end));
  D_Flip_Flop d_ff_5 (.clk(CLK), .D(print_dec_1_end), .Q(WASCII3), .reset(RESET));  // open: Qn, preset, en
  D_Flip_Flop d_ff_6 (.clk(CLK), .D(WASCII3), .Q(d_ff_6_q), .reset(RESET));  // open: Qn, preset, en
  PRINT_DEC print_dec_3 (
    .num(J), .start(d_ff_6_q), .CLK(CLK), .RST(RESET), .ASCII(ASCII4), .Write_ASCII(WASCII4),
    .END(print_dec_3_end));
  or or_4 (or_4_out, print_dec_2_end, print_dec_3_end);
  D_Flip_Flop d_ff_7 (.clk(CLK), .D(or_4_out), .Q(END), .reset(RESET));  // open: Qn, preset, en

  assign LJ = LI;
  assign LN = LI;
endmodule
