// Logisim project BigASM.circ as structural Verilog
module BOARD_BIG_ASM (
  output out_1
);

  wire button_1_out, CLK, CLR, d_ff_1_q, not_1_out, Write, Write_ASCII;
  wire [6:0] ASCII;
  wire [7:0] counter_1_q;
  wire [23:0] Dir_INPUT, Dir_MEMORY;
  wire [31:0] INPUT, MEMORY_IN, MEMORY_OUT;

  Button button_1 (.out(button_1_out));
  Clock clock_1 (.out(CLK));
  D_Flip_Flop d_ff_1 (.clk(CLK), .D(1'b1), .Q(d_ff_1_q), .reset(button_1_out));  // open: Qn, preset, en
  D_Flip_Flop d_ff_2 (.clk(CLK), .D(d_ff_1_q), .Qn(CLR), .reset(button_1_out));  // open: Q, preset, en
  BIG_ASM big_asm_1 (
    .DATA_INPUT(INPUT), .MEMORY_IN(MEMORY_OUT), .CLK(CLK), .CLR(CLR), .DIR_INPUT(Dir_INPUT),
    .MEMORY_OUT(MEMORY_IN), .DIR_MEMORY(Dir_MEMORY), .Write_OUTPUT(Write), .ASCII(ASCII),
    .Write_ASCII(Write_ASCII), .END(out_1));
  MEMORY memory_1 (.DIR(Dir_MEMORY), .DATA_IN(MEMORY_IN), .WRITE(Write), .CLK(CLK), .CLR(CLR), .DATA_OUT(MEMORY_OUT));
  INPUT input_1 (.DIR(Dir_INPUT), .CLK(CLK), .DATA_OUT(INPUT));
  Counter counter_1 (.load(1'b0), .count(not_1_out), .Q(counter_1_q), .clk(CLK), .clr(CLR));  // open: D, carry
  not not_1 (not_1_out, out_1);
  // Probe on counter_1_q
  TTY #(.rows(32), .cols(60)) tty_1 (.data(ASCII), .clk(CLK), .we(Write_ASCII), .clr(CLR));

  // Other names for the same wires on the sheet: END = out_1

  // Notes on the sheet:
  //   COUNTER
  //   BOARD
endmodule

module INPUT (
  input  [23:0] DIR,
  input  CLK,
  output [31:0] DATA_OUT
);

  RAM #(.addrWidth(24), .dataWidth(32)) ram_1 (.addr(DIR), .data(DATA_OUT), .clk(CLK), .ld(1'b1));  // open: sel, clr
endmodule

module MEMORY (
  input  [23:0] DIR,
  input  [31:0] DATA_IN,
  input  WRITE,
  input  CLK,
  input  CLR,
  output [31:0] DATA_OUT
);

  // Probe on DATA_OUT
  RAM #(.addrWidth(24), .dataWidth(32), .bus("separate")) ram_1 (
    .addr(DIR), .din(DATA_IN), .data(DATA_OUT), .str(WRITE), .clk(CLK), .clr(CLR));  // open: sel, ld
endmodule

module BIG_ASM (
  input  [31:0] DATA_INPUT,
  input  [31:0] MEMORY_IN,
  input  CLK,
  input  CLR,
  output [23:0] DIR_INPUT,
  output [31:0] MEMORY_OUT,
  output [23:0] DIR_MEMORY,
  output Write_OUTPUT,
  output [6:0] ASCII,
  output Write_ASCII,
  output END
);

  wire control_unit_1_load___a, control_unit_1_load___b, control_unit_1_load__a, control_unit_1_load__b,
       control_unit_1_load__ctor_a, control_unit_1_load_ctor_b, control_unit_1_selector_ctor_b,
       data_path_1_a____b, data_path_1_ctora__limite, data_path_1_ctorb__limite;
  wire [1:0] control_unit_1_selector_contador;
  wire [31:0] data_path_1_a;

  DATA_PATH data_path_1 (
    .in_1(DATA_INPUT), .CLK(CLK), .Load___A(control_unit_1_load___a), .Load___B(control_unit_1_load___b),
    .Load__Ctor_A(control_unit_1_load__ctor_a), .Load_Ctor_B(control_unit_1_load_ctor_b),
    .Selector_Ctor_B(control_unit_1_selector_ctor_b), .Load__A(control_unit_1_load__a),
    .SC(control_unit_1_selector_contador), .Load__B(control_unit_1_load__b), .A(data_path_1_a),
    .A____B(data_path_1_a____b), .CtorA__Limite(data_path_1_ctora__limite),
    .CtorB__Limite(data_path_1_ctorb__limite), .Contador(DIR_INPUT), .CLR(CLR));
  CONTROL_UNIT control_unit_1 (
    .Clock(CLK), .A____B(data_path_1_a____b), .Load___A(control_unit_1_load___a),
    .Load___B(control_unit_1_load___b), .Load__Ctor_A(control_unit_1_load__ctor_a),
    .CtorA__Limite(data_path_1_ctora__limite), .Load_Ctor_B(control_unit_1_load_ctor_b),
    .CtorB__Limite(data_path_1_ctorb__limite), .Selector_Ctor_B(control_unit_1_selector_ctor_b),
    .in_5(data_path_1_a), .Load__A(control_unit_1_load__a), .Load__B(control_unit_1_load__b), .END(END),
    .ASCII(ASCII), .Write_ASCII(Write_ASCII), .Selector_Contador(control_unit_1_selector_contador));

  // Other names for the same wires on the sheet: CTOR[23:0] = DIR_INPUT
endmodule

module PRINT_UDEC (
  input  [31:0] num,
  input  start,
  input  CLK,
  input  RST,
  output [6:0] ASCII,
  output Write_ASCII,
  output \end 
);

  wire _0_c, _0_n, demultiplexer_1_out0, demultiplexer_2_out0, demultiplexer_2_out1, demultiplexer_3_out0,
       demultiplexer_3_out1, IDLE_2_q, IDLE_3_q, IDLE_4_q, IDLE_q, Lc, Lc_0, Ln, Ln_0, or_1_out;
  wire [23:0] bit_extender_1_out;
  wire [31:0] c, c___1, c___1_t, divider_1_rem, memory_1_data_out, multiplexer_1_out, multiplexer_2_out,
       multiplexer_3_out, n, n___10, n___10___48;

  Multiplexer #(.width(32), .enable("false")) multiplexer_1 (
    .in0(num), .in1(n___10), .out(multiplexer_1_out), .sel(Lc_0));
  Divider #(.width(32)) divider_1 (.a(n), .b(32'ha), .out(n___10), .rem(divider_1_rem));  // open: upper
  Adder #(.width(32)) adder_1 (.a(divider_1_rem), .b(32'h30), .out(n___10___48));  // open: cin, cout
  or or_1 (or_1_out, demultiplexer_1_out0, \end );
  Register #(.width(32)) u_n (.D(multiplexer_1_out), .en(Ln), .Q(n), .clk(CLK), .clr(RST));
  D_Flip_Flop IDLE (.clk(CLK), .D(or_1_out), .Q(IDLE_q), .preset(RST));  // open: Qn, en, reset
  Demultiplexer #(.enable("false")) demultiplexer_1 (
    .out0(demultiplexer_1_out0), .out1(Ln_0), .in(IDLE_q), .sel(start));
  or or_2 (Write_ASCII, demultiplexer_3_out0, demultiplexer_2_out1);
  Multiplexer #(.width(32), .enable("false")) multiplexer_2 (
    .in0(c___1), .in1(c___1_t), .out(multiplexer_2_out), .sel(Write_ASCII));
  Adder #(.width(32)) adder_2 (.a(c), .b(32'h1), .out(c___1));  // open: cin, cout
  Subtractor #(.width(32)) subtractor_1 (.a(c), .b(32'h1), .out(c___1_t));  // open: bin, bout
  D_Flip_Flop IDLE_2 (.clk(CLK), .D(Ln_0), .Q(IDLE_2_q), .reset(RST));  // open: Qn, preset, en
  Register #(.width(32)) u_c (.D(multiplexer_2_out), .en(Lc), .Q(c), .clk(CLK), .clr(RST));
  or or_3 (Lc_0, IDLE_2_q, demultiplexer_3_out1);
  Multiplexer #(.width(32), .enable("false")) multiplexer_3 (
    .in0(c), .in1(c___1_t), .out(multiplexer_3_out), .sel(Write_ASCII));
  Comparator #(.width(32), .mode("unsigned")) comparator_1 (.a({32{1'b0}}), .b(n), .lt(_0_n));  // open: gt, eq
  Comparator #(.width(32), .mode("unsigned")) comparator_2 (.a({32{1'b0}}), .b(c), .lt(_0_c));  // open: gt, eq
  D_Flip_Flop IDLE_3 (.clk(CLK), .D(Write_ASCII), .Q(IDLE_3_q), .reset(RST));  // open: Qn, preset, en
  Demultiplexer #(.enable("false")) demultiplexer_2 (
    .out0(demultiplexer_2_out0), .out1(demultiplexer_2_out1), .in(IDLE_3_q), .sel(_0_c));
  Bit_Extender #(.in_width(32), .out_width(24)) bit_extender_1 (.in(multiplexer_3_out), .out(bit_extender_1_out));
  D_Flip_Flop IDLE_4 (.clk(CLK), .D(Lc_0), .Q(IDLE_4_q), .reset(RST));  // open: Qn, preset, en
  or or_4 (Lc, Lc_0, Write_ASCII);
  or or_5 (Ln, Ln_0, Lc_0);
  Demultiplexer #(.enable("false")) demultiplexer_3 (
    .out0(demultiplexer_3_out0), .out1(demultiplexer_3_out1), .in(IDLE_4_q), .sel(_0_n));
  D_Flip_Flop IDLE_5 (.clk(CLK), .D(demultiplexer_2_out0), .Q(\end ), .reset(RST));  // open: Qn, preset, en
  MEMORY memory_1 (
    .DIR(bit_extender_1_out), .DATA_IN(n___10___48), .WRITE(Lc_0), .CLK(CLK), .CLR(RST),
    .DATA_OUT(memory_1_data_out));
  Bit_Extender #(.in_width(32), .out_width(7)) bit_extender_2 (.in(memory_1_data_out), .out(ASCII));

  // Other names for the same wires on the sheet: Lc_1 = Write_ASCII; Sc = Write_ASCII; Ln_1 = Lc_0; Sn = Lc_0;
  //   Write = Lc_0
endmodule

module PRINT_DEC (
  input  [31:0] num,
  input  start,
  input  CLK,
  input  RST,
  output [6:0] ASCII,
  output Write_ASCII,
  output END
);

  wire demultiplexer_1_out0, demultiplexer_1_out1, demultiplexer_2_out0, demultiplexer_3_out0, end_t,
       IDLE_3_q, IDLE_q, or_1_out, or_2_out, or_3_out, S_ASCII, startUDEC, Write_ASCII_1;
  wire [6:0] ASCII_t;
  wire [31:0] multiplexer_1_out, negator_1_out;

  or or_1 (or_1_out, demultiplexer_1_out0, END);
  Negator #(.width(32)) negator_1 (.in(num), .out(negator_1_out));
  D_Flip_Flop IDLE (.clk(CLK), .D(or_1_out), .Q(IDLE_q), .preset(RST));  // open: Qn, en, reset
  Demultiplexer #(.enable("false")) demultiplexer_1 (
    .out0(demultiplexer_1_out0), .out1(demultiplexer_1_out1), .in(IDLE_q), .sel(start));
  Multiplexer #(.width(32), .enable("false")) multiplexer_1 (
    .in0(num), .in1(negator_1_out), .out(multiplexer_1_out), .sel(num[31]));
  Demultiplexer #(.enable("false")) demultiplexer_2 (
    .out0(demultiplexer_2_out0), .out1(S_ASCII), .in(demultiplexer_1_out1), .sel(num[31]));
  or or_2 (or_2_out, demultiplexer_2_out0, S_ASCII);
  D_Flip_Flop IDLE_2 (.clk(CLK), .D(or_2_out), .Q(startUDEC), .reset(RST));  // open: Qn, preset, en
  PRINT_UDEC print_udec_1 (
    .num(multiplexer_1_out), .start(startUDEC), .CLK(CLK), .RST(RST), .ASCII(ASCII_t),
    .Write_ASCII(Write_ASCII_1), .\end (end_t));
  D_Flip_Flop IDLE_3 (.clk(CLK), .D(or_3_out), .Q(IDLE_3_q), .reset(RST));  // open: Qn, preset, en
  or or_3 (or_3_out, startUDEC, demultiplexer_3_out0);
  Demultiplexer #(.enable("false")) demultiplexer_3 (
    .out0(demultiplexer_3_out0), .out1(END), .in(IDLE_3_q), .sel(end_t));
  Multiplexer #(.width(7), .enable("false")) multiplexer_2 (
    .in0(ASCII_t), .in1(7'b0101101), .out(ASCII), .sel(S_ASCII));
  or or_4 (Write_ASCII, S_ASCII, Write_ASCII_1);

  // Other names for the same wires on the sheet: sign = num[31]; Write_ASCII_0 = S_ASCII
endmodule

module TEST_PRINT (
  input  [31:0] in_1,
  output out_2
);

  wire button_1_out, button_2_out, CLK, CLR, d_ff_1_q, Write_ASCII;
  wire [6:0] ASCII;

  Button button_1 (.out(button_1_out));
  Clock clock_1 (.out(CLK));
  D_Flip_Flop d_ff_1 (.clk(CLK), .D(1'b1), .Q(d_ff_1_q), .reset(button_1_out));  // open: Qn, preset, en
  D_Flip_Flop d_ff_2 (.clk(CLK), .D(d_ff_1_q), .Qn(CLR), .reset(button_1_out));  // open: Q, preset, en
  Button button_2 (.out(button_2_out));
  PRINT_UDEC print_udec_1 ();  // open: num, start, CLK, RST, ASCII, Write_ASCII, end
  PRINT_DEC print_dec_1 (
    .num(in_1), .start(button_2_out), .CLK(CLK), .RST(CLR), .ASCII(ASCII), .Write_ASCII(Write_ASCII),
    .END(out_2));
  TTY #(.rows(32), .cols(60)) tty_1 (.data(ASCII), .clk(CLK), .we(Write_ASCII), .clr(CLR));
endmodule

module DATA_PATH (
  input  [31:0] in_1,
  input  CLK,
  input  Load___A,
  input  Load___B,
  input  Load__Ctor_A,
  input  Load_Ctor_B,
  input  Selector_Ctor_B,
  input  Load__A,
  input  [1:0] SC,
  input  Load__B,
  input  CLR,
  output [31:0] A,
  output A____B,
  output CtorA__Limite,
  output CtorB__Limite,
  output [23:0] Contador
);

  wire [23:0] A____1, B____1, Ctor_A, Ctor_A__1, Ctor_B, Ctor_B__1, Inicio_B, Inicio_B__1, Limite_Ctor_B,
       multiplexer_1_out;
  wire [31:0] A_t, B, B_t, INPUT_t;

  Register #(.width(32)) Cardinalidad_A (.D(INPUT_t), .en(Load___A), .Q(A_t), .clk(CLK), .clr(CLR));
  Register #(.width(32)) Cardinalidad_B (.D(INPUT_t), .en(Load___B), .Q(B_t), .clk(CLK), .clr(CLR));
  Adder #(.width(24)) adder_1 (.a(Ctor_A), .b(24'h1), .out(Ctor_A__1));  // open: cin, cout
  Adder #(.width(24)) adder_2 (.a(Ctor_B), .b(24'h1), .out(Ctor_B__1));  // open: cin, cout
  Adder #(.width(24)) adder_3 (.a(A_t[23:0]), .b(24'h1), .out(A____1));  // open: cin, cout
  Adder #(.width(24)) adder_4 (.a(B_t[23:0]), .b(24'h1), .out(B____1));  // open: cin, cout
  Adder #(.width(24)) adder_5 (.a(A____1), .b(B____1), .out(Limite_Ctor_B));  // open: cin, cout
  Multiplexer #(.width(24), .enable("false")) multiplexer_1 (
    .in0(Inicio_B__1), .in1(Ctor_B__1), .out(multiplexer_1_out), .sel(Selector_Ctor_B));
  Adder #(.width(24)) adder_6 (.a(A_t[23:0]), .b(24'h1), .out(Inicio_B));  // open: cin, cout
  Adder #(.width(24)) adder_7 (.a(Inicio_B), .b(24'h1), .out(Inicio_B__1));  // open: cin, cout
  Register #(.width(24)) u_Ctor_A (.D(Ctor_A__1), .en(Load__Ctor_A), .Q(Ctor_A), .clk(CLK), .clr(CLR));
  Register #(.width(24)) u_Ctor_B (.D(multiplexer_1_out), .en(Load_Ctor_B), .Q(Ctor_B), .clk(CLK), .clr(CLR));
  Multiplexer #(.select(2), .width(24), .enable("false")) multiplexer_2 (
    .in0(Ctor_A), .in1(Inicio_B), .in2(Ctor_B), .out(Contador), .sel(SC));  // open: in3
  Register #(.width(32)) u_A (.D(INPUT_t), .en(Load__A), .Q(A), .clk(CLK), .clr(CLR));
  Register #(.width(32)) u_B (.D(INPUT_t), .en(Load__B), .Q(B), .clk(CLK), .clr(CLR));
  Comparator #(.width(32)) comparator_1 (.a(A), .b(B), .eq(A____B));  // open: gt, lt
  Comparator #(.width(24)) comparator_2 (.a(Ctor_A), .b(A____1), .eq(CtorA__Limite));  // open: gt, lt
  Comparator #(.width(24)) comparator_3 (.a(Ctor_B), .b(Limite_Ctor_B), .eq(CtorB__Limite));  // open: gt, lt
  // Probe on Contador

  // Other names for the same wires on the sheet: INPUT[31:0] = in_1; L_A = Load___A; L_B = Load___B; LA = Load__A;
  //   LB = Load__B; LCA = Load__Ctor_A; LCB = Load_Ctor_B; SCB = Selector_Ctor_B
endmodule

module CONTROL_UNIT (
  input  Clock,
  input  A____B,
  input  CtorA__Limite,
  input  CtorB__Limite,
  input  [31:0] in_5,
  output END,
  output [6:0] ASCII,
  output Load___A,
  output Load___B,
  output Write_ASCII,
  output Load__Ctor_A,
  output Load_Ctor_B,
  output Selector_Ctor_B,
  output Load__A,
  output Load__B,
  output [1:0] Selector_Contador
);

  wire Continuacion1, d_ff_1_q, d_ff_6_q, d_ff_7_q, d_ff_9_q, d_ff_11_q, d_ff_13_q, demultiplexer_1_out0,
       demultiplexer_1_out1, demultiplexer_4_out0, demultiplexer_4_out1, LCA, LCA1, LCB, or_1_out, or_2_out,
       print_dec_1_end, RESET, Selector_Ascii, START, Write_ascii_t;
  wire [6:0] ascii_t;

  Demultiplexer #(.enable("false")) demultiplexer_1 (
    .out0(demultiplexer_1_out0), .out1(demultiplexer_1_out1), .in(d_ff_1_q), .sel(START));
  D_Flip_Flop d_ff_1 (.clk(Clock), .D(demultiplexer_1_out0), .Q(d_ff_1_q), .preset(RESET));  // open: Qn, en, reset
  D_Flip_Flop d_ff_2 (.Q(START), .Qn(RESET), .preset(Clock));  // open: clk, D, en, reset
  or or_1 (or_1_out, Continuacion1, d_ff_9_q);
  D_Flip_Flop d_ff_3 (.clk(Clock), .D(demultiplexer_1_out1), .Q(Load___A), .reset(RESET));  // open: Qn, preset, en
  Demultiplexer #(.enable("false")) demultiplexer_2 (.out0(Load__A), .out1(END), .in(or_1_out), .sel(CtorA__Limite));
  D_Flip_Flop d_ff_4 (.clk(Clock), .D(Load___A), .Q(LCA), .reset(RESET));  // open: Qn, preset, en
  D_Flip_Flop d_ff_5 (.clk(Clock), .D(Load__A), .Q(LCB), .reset(RESET));  // open: Qn, preset, en
  D_Flip_Flop d_ff_6 (.clk(Clock), .D(LCA), .Q(d_ff_6_q), .reset(RESET));  // open: Qn, preset, en
  or or_2 (or_2_out, Selector_Ctor_B, LCB);
  D_Flip_Flop d_ff_7 (.clk(Clock), .D(or_2_out), .Q(d_ff_7_q), .reset(RESET));  // open: Qn, preset, en
  Demultiplexer #(.enable("false")) demultiplexer_3 (.out0(Load__B), .out1(LCA1), .in(d_ff_7_q), .sel(CtorB__Limite));
  D_Flip_Flop d_ff_8 (.clk(Clock), .D(d_ff_6_q), .Q(Load___B), .reset(RESET));  // open: Qn, preset, en
  D_Flip_Flop d_ff_9 (.clk(Clock), .D(LCA1), .Q(d_ff_9_q), .reset(RESET));  // open: Qn, preset, en
  D_Flip_Flop d_ff_10 (.clk(Clock), .D(Load___B), .Q(Continuacion1), .reset(RESET));  // open: Qn, preset, en
  or or_3 (Write_ASCII, Write_ascii_t, Selector_Ascii);
  D_Flip_Flop d_ff_11 (.clk(Clock), .D(Load__B), .Q(d_ff_11_q), .reset(RESET));  // open: Qn, preset, en
  Demultiplexer #(.enable("false")) demultiplexer_4 (
    .out0(demultiplexer_4_out0), .out1(demultiplexer_4_out1), .in(d_ff_11_q), .sel(A____B));
  PRINT_DEC print_dec_1 (
    .num(in_5), .start(demultiplexer_4_out1), .CLK(Clock), .RST(RESET), .ASCII(ascii_t),
    .Write_ASCII(Write_ascii_t), .END(print_dec_1_end));
  or or_4 (Load__Ctor_A, LCA, LCA1);
  or or_5 (Load_Ctor_B, LCB, Selector_Ctor_B);
  or or_6 (Selector_Ctor_B, demultiplexer_4_out0, d_ff_13_q);
  Multiplexer #(.width(7)) multiplexer_1 (
    .in0(ascii_t), .in1(7'b0100000), .out(ASCII), .sel(Selector_Ascii));  // open: en
  D_Flip_Flop d_ff_12 (.clk(Clock), .D(print_dec_1_end), .Q(Selector_Ascii), .reset(RESET));  // open: Qn, preset, en
  D_Flip_Flop d_ff_13 (.clk(Clock), .D(Selector_Ascii), .Q(d_ff_13_q), .reset(RESET));  // open: Qn, preset, en

  assign Selector_Contador = {Load__B, Load___B};

  // Other names for the same wires on the sheet: A[31:0] = in_5; A__B = A____B; CLK = Clock; L_A = Load___A;
  //   LA = Load__A; LCB1 = Selector_Ctor_B; SCB = Selector_Ctor_B; L_B = Load___B; SC1 = Load___B; LB = Load__B;
  //   SC0 = Load__B; Write_ascii_1 = Selector_Ascii
endmodule
